// Logisim project ControlUnit_Flows.circ as structural Verilog: 12 circuits, main circuit ControlUnit
module ControlUnit (
  input  [5:0] OpCode,
  input  [5:0] Funct,
  output RegWirteBack,
  output [3:0] ALUop,
  output JAl,
  output [1:0] PcControl,
  output BEQ,
  output [1:0] W_num,
  output BNE,
  output R1_num,
  output SysCall,
  output [1:0] ALUsrc,
  output [1:0] RF_Din,
  output MemWrite
);

  wire [1:0] bit_extender_1_out, not_1_out, pccontrol_1_out_3;

  PcControl pccontrol_1 (.OpCode(OpCode), .out_3(pccontrol_1_out_3), .Funct(Funct));
  RegW_Dst regw_dst_1 (.OpCode(OpCode), .Funct(Funct), .out_3(W_num));
  RegR1_Dst regr1_dst_1 (.OpCode(OpCode), .Funct(Funct), .out_3(R1_num));
  MemWrite memwrite_1 (.OpCode(OpCode), .Funct(Funct), .out_3(MemWrite));
  assign bit_extender_1_out = {{1{SysCall}}, SysCall};  // Bit_Extender bit_extender_1
  assign not_1_out = ~bit_extender_1_out;  // NOT_Gate not_1, 2 bits wide
  assign PcControl = pccontrol_1_out_3 & not_1_out;  // AND_Gate and_1, 2 bits wide
  RF_Din rf_din_1 (.OpCode(OpCode), .Funct(Funct), .out_3(RF_Din));
  ALUop aluop_1 (.OpCode(OpCode), .Funct(Funct), .out_3(ALUop));
  RegWB regwb_1 (.OpCode(OpCode), .Funct(Funct), .out_3(RegWirteBack));
  ALUsrc alusrc_1 (.OpCode(OpCode), .Funct(Funct), .out_3(ALUsrc));
  SysCall syscall_1 (.OpCode(OpCode), .Funct(Funct), .out_3(SysCall));
  BEQ_BNE beq_bne_1 (.OpCode(OpCode), .Funct(Funct), .out_3({BEQ, BNE}));
  JAL jal_1 (.OpCode(OpCode), .Funct(Funct), .out_3(JAl));

  // Other names for the same wires on the sheet: RegWriteBack = RegWirteBack
endmodule

// PC
module PcControl (
  input  [5:0] OpCode,
  input  [5:0] Funct,
  output [1:0] out_3
);

  wire and_1_out, and_2_out, and_3_out, and_4_out, nFunct0, nFunct1, nFunct2, nFunct3, nFunct4, nFunct5,
       nop0, nop1, nop2, nop3, nop4, nop5, not_13_out, or_1_out;

  not not_1 (nop0, OpCode[0]);
  not not_2 (nop1, OpCode[1]);
  not not_3 (nop2, OpCode[2]);
  not not_4 (nop3, OpCode[3]);
  not not_5 (nop4, OpCode[4]);
  not not_6 (nop5, OpCode[5]);
  not not_7 (nFunct0, Funct[0]);
  not not_8 (nFunct1, Funct[1]);
  not not_9 (nFunct2, Funct[2]);
  not not_10 (nFunct3, Funct[3]);
  not not_11 (nFunct4, Funct[4]);
  not not_12 (nFunct5, Funct[5]);
  not not_13 (not_13_out, or_1_out);
  or or_1 (or_1_out, OpCode[0], OpCode[1], OpCode[2], OpCode[3], OpCode[4], OpCode[5]);
  and and_1 (and_1_out, nop5, nop3, nop2);
  and and_2 (and_2_out, nFunct4, Funct[3], nFunct1);
  Multiplexer #(.enable("false")) multiplexer_1 (.in0(and_1_out), .in1(and_2_out), .out(out_3[1]), .sel(not_13_out));
  and and_3 (and_3_out, nFunct4, Funct[3], nFunct1);
  and and_4 (and_4_out, nop5, nop3, OpCode[2]);
  Multiplexer #(.enable("false")) multiplexer_2 (.in0(and_4_out), .in1(and_3_out), .out(out_3[0]), .sel(not_13_out));

  // Other names for the same wires on the sheet: op0 = OpCode[0]; op1 = OpCode[1]; op2 = OpCode[2]; op3 = OpCode[3];
  //   op4 = OpCode[4]; op5 = OpCode[5]; PcControl[1:0] = out_3
endmodule

module ALUsrc (
  input  [5:0] OpCode,
  input  [5:0] Funct,
  output [1:0] out_3
);

  wire and_1_out, and_2_out, nFunct0, nFunct1, nFunct2, nFunct3, nFunct4, nFunct5, nop0, nop1, nop2, nop3,
       nop4, nop5, not_13_out, or_1_out, or_2_out;

  not not_1 (nop0, OpCode[0]);
  not not_2 (nop1, OpCode[1]);
  not not_3 (nop2, OpCode[2]);
  not not_4 (nop3, OpCode[3]);
  not not_5 (nop4, OpCode[4]);
  not not_6 (nop5, OpCode[5]);
  not not_7 (nFunct0, Funct[0]);
  not not_8 (nFunct1, Funct[1]);
  not not_9 (nFunct2, Funct[2]);
  not not_10 (nFunct3, Funct[3]);
  not not_11 (nFunct4, Funct[4]);
  not not_12 (nFunct5, Funct[5]);
  or or_1 (or_1_out, OpCode[0], OpCode[1], OpCode[2], OpCode[3], OpCode[4], OpCode[5]);
  not not_13 (not_13_out, or_1_out);
  and and_1 (and_1_out, nFunct5, nFunct3, nFunct2);
  and and_2 (and_2_out, OpCode[3], OpCode[2]);
  Multiplexer #(.enable("false")) multiplexer_1 (.in0(and_2_out), .in1(and_1_out), .out(out_3[1]), .sel(not_13_out));
  or or_2 (or_2_out, nop2, OpCode[5]);
  Multiplexer #(.enable("false")) multiplexer_2 (.in0(or_2_out), .in1(and_1_out), .out(out_3[0]), .sel(not_13_out));

  // Other names for the same wires on the sheet: ALUsrc[1:0] = out_3; op0 = OpCode[0]; op1 = OpCode[1];
  //   op2 = OpCode[2]; op3 = OpCode[3]; op4 = OpCode[4]; op5 = OpCode[5]
endmodule

// RW#
module RegW_Dst (
  input  [5:0] OpCode,
  input  [5:0] Funct,
  output [1:0] out_3
);

  wire and_1_out, nFunct0, nFunct1, nFunct2, nFunct3, nFunct4, nFunct5, nop0, nop1, nop2, nop3, nop4, nop5,
       not_13_out, or_1_out;

  not not_1 (nop0, OpCode[0]);
  not not_2 (nop1, OpCode[1]);
  not not_3 (nop2, OpCode[2]);
  not not_4 (nop3, OpCode[3]);
  not not_5 (nop4, OpCode[4]);
  not not_6 (nop5, OpCode[5]);
  not not_7 (nFunct0, Funct[0]);
  not not_8 (nFunct1, Funct[1]);
  not not_9 (nFunct2, Funct[2]);
  not not_10 (nFunct3, Funct[3]);
  not not_11 (nFunct4, Funct[4]);
  not not_12 (nFunct5, Funct[5]);
  or or_1 (or_1_out, OpCode[0], OpCode[1], OpCode[2], OpCode[3], OpCode[4], OpCode[5]);
  not not_13 (not_13_out, or_1_out);
  Multiplexer #(.enable("false")) multiplexer_1 (.in0(1'b0), .in1(1'b1), .out(out_3[1]), .sel(not_13_out));
  and and_1 (and_1_out, nop5, nop4, nop3, nop2, OpCode[1], OpCode[0]);
  Multiplexer #(.enable("false")) multiplexer_2 (.in0(and_1_out), .in1(1'b0), .out(out_3[0]), .sel(not_13_out));

  // Other names for the same wires on the sheet: op0 = OpCode[0]; op1 = OpCode[1]; op2 = OpCode[2]; op3 = OpCode[3];
  //   op4 = OpCode[4]; op5 = OpCode[5]; RW[1:0] = out_3
endmodule

// R1#
module RegR1_Dst (
  input  [5:0] OpCode,
  input  [5:0] Funct,
  output out_3
);

  wire and_1_out, nFunct0, nFunct1, nFunct2, nFunct3, nFunct4, nFunct5, not_7_out, or_1_out;

  not not_1 (nFunct0, Funct[0]);
  not not_2 (nFunct1, Funct[1]);
  not not_3 (nFunct2, Funct[2]);
  not not_4 (nFunct3, Funct[3]);
  not not_5 (nFunct4, Funct[4]);
  not not_6 (nFunct5, Funct[5]);
  or or_1 (or_1_out, OpCode[0], OpCode[1], OpCode[2], OpCode[3], OpCode[4], OpCode[5]);
  not not_7 (not_7_out, or_1_out);
  and and_1 (and_1_out, nFunct5, nFunct4, nFunct3);
  Multiplexer #(.enable("false")) multiplexer_1 (.in0(1'b0), .in1(and_1_out), .out(out_3), .sel(not_7_out));

  // Other names for the same wires on the sheet: R1_num = out_3
endmodule

// MW
module MemWrite (
  input  [5:0] OpCode,
  input  [5:0] Funct,
  output out_3
);

  wire and_1_out, and_2_out, nop0, nop1, nop2, nop3, nop4, nop5;

  not not_1 (nop0, OpCode[0]);
  not not_2 (nop1, OpCode[1]);
  not not_3 (nop2, OpCode[2]);
  not not_4 (nop3, OpCode[3]);
  not not_5 (nop4, OpCode[4]);
  not not_6 (nop5, OpCode[5]);
  and and_1 (and_1_out, nop1, nop2, OpCode[3], nop4, OpCode[5]);
  or or_1 (out_3, and_1_out, and_2_out);
  and and_2 (and_2_out, OpCode[0], nop2, OpCode[3], nop4, OpCode[5]);

  // Other names for the same wires on the sheet: MemWrite = out_3; op0 = OpCode[0]; op1 = OpCode[1]; op2 = OpCode[2];
  //   op3 = OpCode[3]; op4 = OpCode[4]; op5 = OpCode[5]
endmodule

// RF
module RF_Din (
  input  [5:0] OpCode,
  input  [5:0] Funct,
  output [1:0] out_3
);

  wire and_1_out, jar_out, nFunct0, nFunct1, nFunct2, nFunct3, nFunct4, nFunct5, nop0, nop1, nop2, nop3,
       nop4, nop5, not_13_out, or_1_out;
  wire [1:0] multiplexer_2_out;

  not not_1 (nop0, OpCode[0]);
  not not_2 (nop1, OpCode[1]);
  not not_3 (nop2, OpCode[2]);
  not not_4 (nop3, OpCode[3]);
  not not_5 (nop4, OpCode[4]);
  not not_6 (nop5, OpCode[5]);
  not not_7 (nFunct0, Funct[0]);
  not not_8 (nFunct1, Funct[1]);
  not not_9 (nFunct2, Funct[2]);
  not not_10 (nFunct3, Funct[3]);
  not not_11 (nFunct4, Funct[4]);
  not not_12 (nFunct5, Funct[5]);
  not not_13 (not_13_out, or_1_out);
  or or_1 (or_1_out, OpCode[0], OpCode[1], OpCode[2], OpCode[3], OpCode[4], OpCode[5]);
  Multiplexer #(.enable("false")) multiplexer_1 (
    .in0(1'b0), .in1(Funct[4]), .out(multiplexer_2_out[1]), .sel(not_13_out));
  and and_1 (and_1_out, Funct[4], Funct[1]);
  Multiplexer #(.enable("false")) multiplexer_2 (
    .in0(nop3), .in1(and_1_out), .out(multiplexer_2_out[0]), .sel(not_13_out));
  and jar (jar_out, nop5, nop4, nop3, nop2, OpCode[1], OpCode[0]);
  Multiplexer #(.width(2), .enable("false")) multiplexer_3 (
    .in0(multiplexer_2_out), .in1(2'b00), .out(out_3), .sel(jar_out));

  // Other names for the same wires on the sheet: op0 = OpCode[0]; op1 = OpCode[1]; op2 = OpCode[2]; op3 = OpCode[3];
  //   op4 = OpCode[4]; op5 = OpCode[5]; RF_Din[1:0] = out_3
endmodule

module ALUop (
  input  [5:0] OpCode,
  input  [5:0] Funct,
  output [3:0] out_3
);

  wire and_1_out, and_2_out, and_3_out, and_4_out, and_5_out, and_6_out, and_7_out, and_8_out, and_9_out,
       and_10_out, and_11_out, and_12_out, and_13_out, and_14_out, and_15_out, and_16_out, and_17_out,
       and_18_out, and_19_out, and_20_out, nFunct0, nFunct1, nFunct2, nFunct3, nFunct4, nFunct5, nop0, nop1,
       nop2, nop3, nop4, nop5, not_13_out, or_1_out, or_2_out, or_3_out, or_4_out, or_5_out, or_6_out,
       or_7_out, or_8_out, or_9_out;
  wire [3:0] multiplexer_5_out;

  not not_1 (nop0, OpCode[0]);
  not not_2 (nop1, OpCode[1]);
  not not_3 (nop2, OpCode[2]);
  not not_4 (nop3, OpCode[3]);
  not not_5 (nop4, OpCode[4]);
  not not_6 (nop5, OpCode[5]);
  not not_7 (nFunct0, Funct[0]);
  not not_8 (nFunct1, Funct[1]);
  not not_9 (nFunct2, Funct[2]);
  not not_10 (nFunct3, Funct[3]);
  not not_11 (nFunct4, Funct[4]);
  not not_12 (nFunct5, Funct[5]);
  or or_1 (or_1_out, OpCode[0], OpCode[1], OpCode[2], OpCode[3], OpCode[4], OpCode[5]);
  and and_1 (and_1_out, nop5, OpCode[2], OpCode[0]);
  and and_2 (and_2_out, nop5, OpCode[1]);
  or or_2 (or_2_out, and_2_out, and_1_out);
  not not_13 (not_13_out, or_1_out);
  Multiplexer #(.enable("false")) multiplexer_1 (
    .in0(or_2_out), .in1(or_3_out), .out(multiplexer_5_out[3]), .sel(not_13_out));
  and and_3 (and_3_out, nFunct4, Funct[3]);
  and and_4 (and_4_out, Funct[2], Funct[0]);
  or or_3 (or_3_out, and_4_out, and_3_out);
  and and_5 (and_5_out, nop1, nop0);
  and and_6 (and_6_out, nop2, OpCode[0]);
  or or_4 (or_4_out, and_5_out, nop3, and_6_out);
  and and_7 (and_7_out, Funct[5], nFunct3, nFunct2);
  and and_8 (and_8_out, Funct[2], nFunct0);
  or or_5 (or_5_out, and_8_out, and_7_out, and_9_out);
  Multiplexer #(.enable("false")) multiplexer_2 (
    .in0(or_4_out), .in1(or_5_out), .out(multiplexer_5_out[2]), .sel(not_13_out));
  and and_9 (and_9_out, Funct[3], Funct[0]);
  Multiplexer #(.width(4), .enable("false")) multiplexer_3 (
    .in0(multiplexer_5_out), .in1(4'b0101), .out(out_3), .sel(and_20_out));
  and and_10 (and_10_out, nop5, OpCode[2], nop1, nop0);
  and and_11 (and_11_out, nop2, OpCode[1], nop0);
  or or_6 (or_6_out, and_11_out, and_10_out);
  and and_12 (and_12_out, Funct[1], nFunct0);
  Multiplexer #(.enable("false")) multiplexer_4 (
    .in0(or_6_out), .in1(or_7_out), .out(multiplexer_5_out[1]), .sel(not_13_out));
  and and_13 (and_13_out, Funct[4], nFunct0);
  and and_14 (and_14_out, Funct[2], Funct[1]);
  and and_15 (and_15_out, Funct[2], nFunct0);
  or or_7 (or_7_out, and_12_out, and_15_out, and_14_out, and_13_out);
  and and_16 (and_16_out, nop2, nop1);
  or or_8 (or_8_out, nop0, and_16_out, OpCode[5]);
  and and_17 (and_17_out, nFunct3, nFunct2, Funct[0]);
  Multiplexer #(.enable("false")) multiplexer_5 (
    .in0(or_8_out), .in1(or_9_out), .out(multiplexer_5_out[0]), .sel(not_13_out));
  and and_18 (and_18_out, Funct[3], nFunct0);
  and and_19 (and_19_out, Funct[5], nFunct1, nFunct0);
  or or_9 (or_9_out, and_17_out, and_18_out, and_19_out);
  and and_20 (and_20_out, nop5, nop4, nop3, nop2, OpCode[1], OpCode[0]);

  // Other names for the same wires on the sheet: ALUop[3:0] = out_3; op0 = OpCode[0]; op1 = OpCode[1];
  //   op2 = OpCode[2]; op3 = OpCode[3]; op4 = OpCode[4]; op5 = OpCode[5]
endmodule

module RegWB (
  input  [5:0] OpCode,
  input  [5:0] Funct,
  output out_3
);

  wire and_1_out, and_2_out, and_3_out, and_4_out, and_5_out, and_6_out, and_7_out, and_8_out, and_9_out,
       and_10_out, multiplexer_1_out, nFunct0, nFunct1, nFunct2, nFunct3, nFunct4, nFunct5, nop0, nop1, nop2,
       nop3, nop4, nop5, not_13_out, or_1_out, or_2_out, or_3_out;

  not not_1 (nop0, OpCode[0]);
  not not_2 (nop1, OpCode[1]);
  not not_3 (nop2, OpCode[2]);
  not not_4 (nop3, OpCode[3]);
  not not_5 (nop4, OpCode[4]);
  not not_6 (nop5, OpCode[5]);
  not not_7 (nFunct0, Funct[0]);
  not not_8 (nFunct1, Funct[1]);
  not not_9 (nFunct2, Funct[2]);
  not not_10 (nFunct3, Funct[3]);
  not not_11 (nFunct4, Funct[4]);
  not not_12 (nFunct5, Funct[5]);
  and and_1 (and_1_out, OpCode[5], nop4, nop3, nop2, OpCode[0]);
  and and_2 (and_2_out, nop5, nop4, OpCode[3]);
  or or_1 (or_1_out, and_1_out, and_2_out, and_3_out);
  or or_2 (or_2_out, OpCode[0], OpCode[1], OpCode[2], OpCode[3], OpCode[4], OpCode[5]);
  and and_3 (and_3_out, OpCode[5], nop4, nop3, nop1);
  not not_13 (not_13_out, or_2_out);
  and and_4 (and_4_out, nFunct4, nFunct3, nFunct0);
  and and_5 (and_5_out, nFunct5, nFunct3, nFunct2, nFunct0);
  Multiplexer #(.enable("false")) multiplexer_1 (
    .in0(or_1_out), .in1(or_3_out), .out(multiplexer_1_out), .sel(not_13_out));
  and and_6 (and_6_out, nFunct4, nFunct3, Funct[1]);
  and and_7 (and_7_out, nFunct5, nFunct4, Funct[3], nFunct2, nFunct1, Funct[0]);
  or or_3 (or_3_out, and_5_out, and_4_out, and_6_out, and_7_out, and_9_out, and_8_out);
  and and_8 (and_8_out, Funct[5], nFunct4, nFunct2, Funct[1]);
  and and_9 (and_9_out, Funct[5], nFunct4, nFunct3);
  or or_4 (out_3, multiplexer_1_out, and_10_out);
  and and_10 (and_10_out, nop5, nop4, nop3, nop2, OpCode[0], OpCode[1]);

  // Other names for the same wires on the sheet: op0 = OpCode[0]; op1 = OpCode[1]; op2 = OpCode[2]; op3 = OpCode[3];
  //   op4 = OpCode[4]; op5 = OpCode[5]; RegWB = out_3
endmodule

module SysCall (
  input  [5:0] OpCode,
  input  [5:0] Funct,
  output out_3
);

  wire nFunct0, nFunct1, nFunct2, nFunct3, nFunct4, nFunct5, nop0, nop1, nop2, nop3, nop4, nop5;

  not not_1 (nop0, OpCode[0]);
  not not_2 (nop1, OpCode[1]);
  not not_3 (nop2, OpCode[2]);
  not not_4 (nop3, OpCode[3]);
  not not_5 (nop4, OpCode[4]);
  not not_6 (nop5, OpCode[5]);
  not not_7 (nFunct0, Funct[0]);
  not not_8 (nFunct1, Funct[1]);
  not not_9 (nFunct2, Funct[2]);
  not not_10 (nFunct3, Funct[3]);
  not not_11 (nFunct4, Funct[4]);
  not not_12 (nFunct5, Funct[5]);
  and and_1 (out_3, nop0, nop1, nop2, nop3, nop4, nop5, nFunct0, nFunct1, Funct[2], Funct[3], nFunct4, nFunct4);

  // Other names for the same wires on the sheet: op0 = OpCode[0]; op1 = OpCode[1]; op2 = OpCode[2]; op3 = OpCode[3];
  //   op4 = OpCode[4]; op5 = OpCode[5]; SysCall = out_3
endmodule

module BEQ_BNE (
  input  [5:0] OpCode,
  input  [5:0] Funct,
  output [1:0] out_3
);

  wire and_1_out, and_2_out, nop0, nop1, nop2, nop3, nop4, nop5, not_7_out, or_1_out;

  not not_1 (nop0, OpCode[0]);
  not not_2 (nop1, OpCode[1]);
  not not_3 (nop2, OpCode[2]);
  not not_4 (nop3, OpCode[3]);
  not not_5 (nop4, OpCode[4]);
  not not_6 (nop5, OpCode[5]);
  or or_1 (or_1_out, OpCode[0], OpCode[1], OpCode[2], OpCode[3], OpCode[4], OpCode[5]);
  and and_1 (and_1_out, nop5, nop4, nop3, OpCode[2], nop1, nop0);
  not not_7 (not_7_out, or_1_out);
  Multiplexer #(.enable("false")) multiplexer_1 (.in0(and_1_out), .in1(1'b0), .out(out_3[1]), .sel(not_7_out));
  and and_2 (and_2_out, nop5, nop4, nop3, OpCode[2], nop1, OpCode[0]);
  Multiplexer #(.enable("false")) multiplexer_2 (.in0(and_2_out), .in1(1'b0), .out(out_3[0]), .sel(not_7_out));

  // Other names for the same wires on the sheet: BEQ_BNE[1:0] = out_3; op0 = OpCode[0]; op1 = OpCode[1];
  //   op2 = OpCode[2]; op3 = OpCode[3]; op4 = OpCode[4]; op5 = OpCode[5]
endmodule

module JAL (
  input  [5:0] OpCode,
  input  [5:0] Funct,
  output out_3
);

  wire and_1_out, nop0, nop1, nop2, nop3, nop4, nop5, not_7_out, or_1_out;

  not not_1 (nop0, OpCode[0]);
  not not_2 (nop1, OpCode[1]);
  not not_3 (nop2, OpCode[2]);
  not not_4 (nop3, OpCode[3]);
  not not_5 (nop4, OpCode[4]);
  not not_6 (nop5, OpCode[5]);
  or or_1 (or_1_out, OpCode[0], OpCode[1], OpCode[2], OpCode[3], OpCode[4], OpCode[5]);
  and and_1 (and_1_out, nop5, nop4, nop3, nop2, OpCode[1], OpCode[0]);
  not not_7 (not_7_out, or_1_out);
  Multiplexer #(.enable("false")) multiplexer_1 (.in0(and_1_out), .in1(1'b0), .out(out_3), .sel(not_7_out));

  // Other names for the same wires on the sheet: JAL = out_3; op0 = OpCode[0]; op1 = OpCode[1]; op2 = OpCode[2];
  //   op3 = OpCode[3]; op4 = OpCode[4]; op5 = OpCode[5]
endmodule
