// Logisim project DataMemory.circ as structural Verilog: 1 circuit, main circuit main
module main (
  input  in_1,
  input  [31:0] in_2,
  input  [31:0] in_3,
  input  in_4,
  output [31:0] out_5
);

  RAM #(.addrWidth(24), .dataWidth(32), .bus("separate")) ram_1 (
    .addr(in_3[25:2]), .din(in_2), .data(out_5), .clk(in_1), .ld(in_4));  // open: str, sel, clr

  // Other names for the same wires on the sheet: Addr[31:0] = in_3; Clk = in_1; Data[31:0] = in_2;
  //   DataOut[31:0] = out_5; MemR = in_4
endmodule
