// Logisim project Flows.circ as structural Verilog: 6 circuits, main circuit main
module main (
  input  [4:0] in_1
);

  wire alu_1_equal, and_1_out, Clk, clock_1_out, comparator_1_eq, comparator_2_eq, comparator_3_eq,
       conflictunit_1_c_id_ex_clr, conflictunit_1_conflict, conflictunit_1_jmp, conflictunit_1_stop_clk,
       controlunit_1_beq, controlunit_1_bne, controlunit_1_jal, controlunit_1_memwrite, controlunit_1_r1_num,
       controlunit_1_regwirteback, controlunit_1_syscall, ex_mem_1_memwriteen, ex_mem_1_regwb_2,
       ex_mem_1_syscall_out, hilocontrol_1_hilocontrol, id_ex_1_branch, id_ex_1_memweite_out,
       id_ex_1_regwb_2, id_ex_1_syscall_out, mem_wb_1_regwb_2, not_1_out, not_2_out, not_3_out, not_4_out,
       not_5_out, SysCall;
  wire [1:0] controlunit_1_alusrc, controlunit_1_pccontrol, controlunit_1_rf_din, controlunit_1_w_num,
       ex_mem_1_rf_din_2, id_ex_1_rf_din_out;
  wire [3:0] controlunit_1_aluop, id_ex_1_aluop_out, multiplexer_3_out_2, multiplexer_3_out_3,
       multiplexer_3_out_4, multiplexer_3_out_5;
  wire [4:0] ex_mem_1_regw_num_2, id_ex_1_regw__out, instrdecode_1_rd, instrdecode_1_rs, instrdecode_1_rt,
       instrdecode_1_shamt, mem_wb_1_regw_num_2, multiplexer_4_out, multiplexer_5_out;
  wire [5:0] instrdecode_1_funct, instrdecode_1_opcode;
  wire [15:0] instrdecode_1_imm, multiplexer_3_out;
  wire [23:0] ex_mem_1_addr_2, ex_mem_1_pc_out_2, id_ex_1_pc_out_2, if_id_1_pc_out_2, register_1_q_2;
  wire [25:0] instrdecode_1_addr;
  wire [31:0] a0, adder_1_out, alu_1_result, alu_1_result_2, counter_1_q, counter_2_q, counter_3_q,
       counter_4_q, DebugValue, ex_mem_1_dm_din_2, ex_mem_1_hi_out, ex_mem_1_instr_out, ex_mem_1_lo_out,
       ex_mem_1_pc_out, ex_mem_1_reg_data, hilo_1_hi_out, hilo_1_lo_out, id_ex_1_instr_out, id_ex_1_jmp_addr,
       id_ex_1_pc_out, id_ex_1_r2_out, id_ex_1_x, id_ex_1_y, if_id_1_instr, if_id_1_instr_out,
       if_id_1_pc_out, mem_wb_1_instr_out, mem_wb_1_pc_out, mem_wb_1_wb_data, multiplexer_1_out, ram_1_data,
       regfile_1_reg1, regfile_1_reg2_2, register_1_q, rom_1_data, v0;

  not not_1 (not_1_out, conflictunit_1_stop_clk);
  ConflictUnit conflictunit_1 (
    .Branch(id_ex_1_branch), .R1(multiplexer_4_out), .R2(instrdecode_1_rt), .EX_RWB(id_ex_1_regwb_2),
    .EX_RW_num(id_ex_1_regw__out), .MEM_RWB(ex_mem_1_regwb_2), .MEM_RW_num(ex_mem_1_regw_num_2),
    .EX_Instr(id_ex_1_instr_out), .MEM_Instr(ex_mem_1_instr_out), .Jmp(conflictunit_1_jmp),
    .Conflict(conflictunit_1_conflict), .C_ID_EX_Clr(conflictunit_1_c_id_ex_clr),
    .Stop_Clk(conflictunit_1_stop_clk));  // open: IF_ID_Clr, B_ID_EX_Clr
  Register #(.width(32)) register_1 (
    .D(multiplexer_1_out), .en(not_1_out), .Q({register_1_q[31:26], register_1_q_2, register_1_q[1:0]}),
    .clk(Clk));  // open: clr
  Adder #(.width(32)) adder_1 (
    .a({register_1_q[31:26], register_1_q_2, register_1_q[1:0]}), .b(32'h4), .out(adder_1_out));  // open: cin, cout
  Multiplexer #(.width(32), .enable("false")) multiplexer_1 (
    .in0(adder_1_out), .in1(id_ex_1_jmp_addr), .out(multiplexer_1_out), .sel(id_ex_1_branch));
  // Probe on register_1_q_2
  ROM #(.addrWidth(24), .dataWidth(32)) rom_1 (.addr(register_1_q_2), .data(rom_1_data));  // open: sel
  // Probe on DebugValue
  Comparator #(.width(32)) comparator_1 (.a(v0), .b(32'ha), .eq(comparator_1_eq));  // open: gt, lt
  // Probe on rom_1_data
  IF_ID if_id_1 (
    .Clk(Clk), .Code(rom_1_data), .Instr_Out(if_id_1_instr_out), .Instr(if_id_1_instr),
    .PC_In({register_1_q[31:26], register_1_q_2, register_1_q[1:0]}),
    .PC_Out({if_id_1_pc_out[31:26], if_id_1_pc_out_2, if_id_1_pc_out[1:0]}), .Clr(id_ex_1_branch),
    .Stop_Clk(conflictunit_1_stop_clk));
  // Probe on in_1
  Hex_Digit_Display hex_digit_display_1 (.value(multiplexer_3_out_5));  // open: dp
  and and_1 (and_1_out, comparator_1_eq, SysCall);
  Clock clock_1 (.out(clock_1_out));
  // Probe on if_id_1_instr
  // Probe on if_id_1_pc_out_2
  // Probe on if_id_1_instr_out
  InstrDecode instrdecode_1 (
    .rd(instrdecode_1_rd), .rt(instrdecode_1_rt), .Addr(instrdecode_1_addr), .IMM(instrdecode_1_imm),
    .IND(if_id_1_instr_out), .rs(instrdecode_1_rs), .Funct(instrdecode_1_funct),
    .OpCode(instrdecode_1_opcode), .shamt(instrdecode_1_shamt));
  Hex_Digit_Display hex_digit_display_2 (.value(multiplexer_3_out_3));  // open: dp
  Hex_Digit_Display hex_digit_display_3 (.value(multiplexer_3_out_4));  // open: dp
  Multiplexer #(.enable("false")) multiplexer_2 (.in0(clock_1_out), .in1(1'b0), .out(Clk), .sel(and_1_out));
  Hex_Digit_Display hex_digit_display_4 (.value(multiplexer_3_out[15:12]));  // open: dp
  Hex_Digit_Display hex_digit_display_5 (.value(multiplexer_3_out_2));  // open: dp
  Multiplexer #(.width(32), .enable("false")) multiplexer_3 (
    .in1(a0),
    .out({multiplexer_3_out_5, multiplexer_3_out_4, multiplexer_3_out_3, multiplexer_3_out_2, multiplexer_3_out}),
    .sel(not_2_out));  // open: in0
  not not_2 (not_2_out, and_1_out);
  Multiplexer #(.width(5), .enable("false")) multiplexer_4 (
    .in0(instrdecode_1_rs), .in1(instrdecode_1_rt), .out(multiplexer_4_out), .sel(controlunit_1_r1_num));
  Multiplexer #(.select(2), .width(5), .enable("false")) multiplexer_5 (
    .in0(instrdecode_1_rt), .in1({5{1'b1}}), .in2(instrdecode_1_rd), .out(multiplexer_5_out),
    .sel(controlunit_1_w_num));  // open: in3
  ControlUnit controlunit_1 (
    .RegWirteBack(controlunit_1_regwirteback), .ALUop(controlunit_1_aluop),
    .PcControl(controlunit_1_pccontrol), .W_num(controlunit_1_w_num), .R1_num(controlunit_1_r1_num),
    .RF_Din(controlunit_1_rf_din), .MemWrite(controlunit_1_memwrite), .ALUsrc(controlunit_1_alusrc),
    .SysCall(controlunit_1_syscall), .BNE(controlunit_1_bne), .BEQ(controlunit_1_beq),
    .JAl(controlunit_1_jal), .OpCode(instrdecode_1_opcode), .Funct(instrdecode_1_funct));
  Hex_Digit_Display hex_digit_display_6 (.value(multiplexer_3_out[11:8]));  // open: dp
  Hex_Digit_Display hex_digit_display_7 (.value(multiplexer_3_out[7:4]));  // open: dp
  Hex_Digit_Display hex_digit_display_8 (.value(multiplexer_3_out[3:0]));  // open: dp
  not not_3 (not_3_out, comparator_2_eq);
  RegFile regfile_1 (
    .Reg1_num(multiplexer_4_out), .Reg2(instrdecode_1_rt), .Write_Reg_num(mem_wb_1_regw_num_2),
    .Din(mem_wb_1_wb_data), .Write_Enable(mem_wb_1_regwb_2), .Clock(not_4_out), .Reg1(regfile_1_reg1),
    .Reg2_2(regfile_1_reg2_2), .v0(v0), .a0(a0), .in_3(in_1), .DebugValue(DebugValue));
  not not_4 (not_4_out, Clk);
  Counter #(.width(32), .max('hffffffff), .trigger("falling")) counter_1 (
    .load(comparator_2_eq), .D(32'h2), .count(not_3_out), .Q(counter_1_q), .clk(Clk));  // open: carry, clr
  // Probe on counter_1_q
  // Probe on id_ex_1_pc_out_2
  ID_EX id_ex_1 (
    .in_1(Clk), .Instr_In(if_id_1_instr), .Instr_Out(id_ex_1_instr_out), .R1(regfile_1_reg1),
    .R2(regfile_1_reg2_2), .PC_In({if_id_1_pc_out[31:26], if_id_1_pc_out_2, if_id_1_pc_out[1:0]}),
    .PC_Out({id_ex_1_pc_out[31:26], id_ex_1_pc_out_2, id_ex_1_pc_out[1:0]}), .shmat(instrdecode_1_shamt),
    .IMM(instrdecode_1_imm), .JAL(controlunit_1_jal), .ALUsrc(controlunit_1_alusrc), .X(id_ex_1_x),
    .Y(id_ex_1_y), .ALUop(controlunit_1_aluop), .Addr(instrdecode_1_addr), .RegW_num(multiplexer_5_out),
    .RegWB(controlunit_1_regwirteback), .RF_Din(controlunit_1_rf_din), .MemWrite(controlunit_1_memwrite),
    .MemWeite_Out(id_ex_1_memweite_out), .ALUop_Out(id_ex_1_aluop_out), .RegW__Out(id_ex_1_regw__out),
    .RegWB_2(id_ex_1_regwb_2), .RF_Din_Out(id_ex_1_rf_din_out), .PcControl(controlunit_1_pccontrol),
    .BNE(controlunit_1_bne), .BEQ(controlunit_1_beq), .R2_Out(id_ex_1_r2_out), .EQUAL(alu_1_equal),
    .Branch(id_ex_1_branch), .JMP_addr(id_ex_1_jmp_addr), .SysCall(controlunit_1_syscall),
    .SysCall_Out(id_ex_1_syscall_out), .C_Clr(conflictunit_1_c_id_ex_clr), .B_Clr(id_ex_1_branch));
  Comparator #(.width(32)) comparator_2 (.a(counter_1_q), .b({32{1'b0}}), .eq(comparator_2_eq));  // open: gt, lt
  // Probe on id_ex_1_instr_out
  HILOControl hilocontrol_1 (.ALUop(id_ex_1_aluop_out), .HILOControl(hilocontrol_1_hilocontrol));
  ALU alu_1 (
    .AluOP(id_ex_1_aluop_out), .X(id_ex_1_x), .Equal(alu_1_equal), .Result(alu_1_result), .Y(id_ex_1_y),
    .Result_2(alu_1_result_2));  // open: Signed_Overflow, UnSigned_Overflow
  HILO hilo_1 (
    .HI_In(alu_1_result_2), .LO_In(alu_1_result), .Clk(Clk), .Control(hilocontrol_1_hilocontrol),
    .HI_Out(hilo_1_hi_out), .LO_Out(hilo_1_lo_out));
  Counter #(.width(32), .max('hffffffff)) counter_2 (
    .count(conflictunit_1_jmp), .Q(counter_2_q), .clk(Clk));  // open: load, D, carry, clr
  Counter #(.width(32), .max('hffffffff)) counter_3 (
    .load(1'b0), .count(conflictunit_1_conflict), .Q(counter_3_q), .clk(Clk));  // open: D, carry, clr
  // Probe on ex_mem_1_pc_out_2
  EX_MEM ex_mem_1 (
    .in_1(Clk), .Instr_In(id_ex_1_instr_out),
    .PC_In({id_ex_1_pc_out[31:26], id_ex_1_pc_out_2, id_ex_1_pc_out[1:0]}), .Instr_Out(ex_mem_1_instr_out),
    .PC_Out({ex_mem_1_pc_out[31:26], ex_mem_1_pc_out_2, ex_mem_1_pc_out[1:0]}), .Addr(alu_1_result),
    .Reg_Data(ex_mem_1_reg_data), .Addr_2(ex_mem_1_addr_2), .DM_Din(id_ex_1_r2_out),
    .DM_Din_2(ex_mem_1_dm_din_2), .MemWrite(id_ex_1_memweite_out), .MemWriteEn(ex_mem_1_memwriteen),
    .RF_Din(id_ex_1_rf_din_out), .RF_Din_2(ex_mem_1_rf_din_2), .LO_In(hilo_1_lo_out), .HI_In(hilo_1_hi_out),
    .HI_Out(ex_mem_1_hi_out), .LO_Out(ex_mem_1_lo_out), .RegW_num(id_ex_1_regw__out),
    .RegWB(id_ex_1_regwb_2), .RegWB_2(ex_mem_1_regwb_2), .RegW_num_2(ex_mem_1_regw_num_2),
    .SysCall(id_ex_1_syscall_out), .SysCall_Out(ex_mem_1_syscall_out));
  // Probe on counter_2_q
  // Probe on counter_3_q
  // Probe on ex_mem_1_instr_out
  not not_5 (not_5_out, Clk);
  Comparator #(.width(32)) comparator_3 (.a({32{1'b0}}), .b(mem_wb_1_instr_out), .eq(comparator_3_eq));  // open: gt, lt
  RAM #(.addrWidth(24), .dataWidth(32), .bus("separate")) ram_1 (
    .addr(ex_mem_1_addr_2), .din(ex_mem_1_dm_din_2), .data(ram_1_data), .str(ex_mem_1_memwriteen),
    .clk(not_5_out), .ld(ex_mem_1_rf_din_2[0]));  // open: sel, clr
  Counter #(.width(32), .max('hffffffff)) counter_4 (
    .count(comparator_3_eq), .Q(counter_4_q), .clk(Clk));  // open: load, D, carry, clr
  // Probe on mem_wb_1_pc_out[25:2]
  MEM_WB mem_wb_1 (
    .LO_In(ex_mem_1_lo_out), .HI_In(ex_mem_1_hi_out), .Clk(Clk), .Reg_Data(ex_mem_1_reg_data),
    .DM_Out(ram_1_data), .RF_Din(ex_mem_1_rf_din_2), .WB_data(mem_wb_1_wb_data), .RegWB(ex_mem_1_regwb_2),
    .RegW_num(ex_mem_1_regw_num_2), .RegWB_2(mem_wb_1_regwb_2), .RegW_num_2(mem_wb_1_regw_num_2),
    .Instr_Out(mem_wb_1_instr_out), .PC_Out(mem_wb_1_pc_out), .Instr_In(ex_mem_1_instr_out),
    .PC_In({ex_mem_1_pc_out[31:26], ex_mem_1_pc_out_2, ex_mem_1_pc_out[1:0]}),
    .SysCall(ex_mem_1_syscall_out), .SYSCALL_2(SysCall));
  // Probe on counter_4_q
  // Probe on mem_wb_1_instr_out

  // Other names for the same wires on the sheet: Debug[4:0] = in_1

  // Notes on the sheet:
  //   contents of rom_1 (hex, n*v repeats v):
  //   20110001 8000c05 20110001 20120002 20130003 8000c09 20110001 20120002 20130003 8000c0d 20110001
  //   20120002 20130003 8000c11 20110001 20120002 20130003 c000cce 20110001 20120010 112020 20020022 c
  //   2320018 4810 8812 112020 20020022 c 1120fff9 20110001 20120010 118fc0 112020 20020022 c 232001b 4810
  //   8812 1620fff9 20100001 20110001 118fc0 112020 20020022 c 118882 12200001 8000c2b 112020 20020022 c
  //   20110001 118880 112020 20020022 c 12200001 8000c35 20110001 118fc0 112020 20020022 c 1188c3 112020
  //   20020022 c 118903 112020 20020022 c 118903 112020 20020022 c 118903 112020 20020022 c 118903 112020
  //   20020022 c 118903 112020 20020022 c 118903 112020 20020022 c 118903 112020 20020022 c 20100001
  //   109fc0 139fc3 8021 2012000c 24160003 26100001 3210000f 20080008 20090001 139900 2709825 132020
  //   20020022 c 1094022 1500fff9 22100001 2018000f 2188024 108700 20080008 20090001 139902 2709825 132021
  //   20020022 c 1094022 1500fff9 108702 2c9b022 12c00001 8000c66 4020 1084027 84400 3508ffff 82021
  //   20020022 c 2010ffff 20110000 ae300000 22100001 22310004 ae300000 22100001 22310004 ae300000 22100001
  //   22310004 ae300000 22100001 22310004 ae300000 22100001 22310004 ae300000 22100001 22310004 ae300000
  //   22100001 22310004 ae300000 22100001 22310004 ae300000 22100001 22310004 ae300000 22100001 22310004
  //   ae300000 22100001 22310004 ae300000 22100001 22310004 ae300000 22100001 22310004 ae300000 22100001
  //   22310004 ae300000 22100001 22310004 ae300000 22100001 22310004 22100001 8020 2011003c 8e130000
  //   8e340000 274402a 11000002 ae330000 ae140000 2231fffc 1611fff8 102020 20020022 c 22100004 2011003c
  //   1611fff2 2002000a c 20100000 22100001 102020 20020022 c 22100002 102020 20020022 c 22100003 102020
  //   20020022 c 22100004 102020 20020022 c 22100005 102020 20020022 c 22100006 102020 20020022 c 22100007
  //   102020 20020022 c 22100008 102020 20020022 20020022 c 3e00008
endmodule

module IF_ID (
  input  Clk,
  input  Clr,
  input  Stop_Clk,
  input  [31:0] Code,
  input  [31:0] PC_In,
  output [31:0] Instr_Out,
  output [31:0] Instr,
  output [31:0] PC_Out
);

  wire not_1_out;
  wire [31:0] multiplexer_1_out, multiplexer_2_out;

  // Probe on Code
  // Probe on PC_In
  Multiplexer #(.width(32), .enable("false")) multiplexer_1 (
    .in0(Code), .in1({32{1'b0}}), .out(multiplexer_1_out), .sel(Clr));
  Multiplexer #(.width(32), .enable("false")) multiplexer_2 (
    .in0(PC_In), .in1({32{1'b0}}), .out(multiplexer_2_out), .sel(Clr));
  not not_1 (not_1_out, Stop_Clk);
  Register #(.width(32)) register_1 (.D(multiplexer_1_out), .en(not_1_out), .Q(Instr), .clk(Clk));  // open: clr
  Register #(.width(32)) register_2 (.D(multiplexer_2_out), .en(not_1_out), .Q(PC_Out), .clk(Clk));  // open: clr

  assign Instr_Out = Instr;
endmodule

module ID_EX (
  input  in_1,
  input  JAL,
  input  C_Clr,
  input  B_Clr,
  input  MemWrite,
  input  EQUAL,
  input  BNE,
  input  BEQ,
  input  [3:0] ALUop,
  input  [1:0] PcControl,
  input  RegWB,
  input  SysCall,
  input  [4:0] RegW_num,
  input  [1:0] RF_Din,
  input  [25:0] Addr,
  input  [31:0] PC_In,
  input  [31:0] Instr_In,
  input  [31:0] R1,
  input  [31:0] R2,
  input  [15:0] IMM,
  input  [4:0] shmat,
  input  [1:0] ALUsrc,
  output [31:0] Instr_Out,
  output [31:0] PC_Out,
  output [31:0] X,
  output [31:0] Y,
  output [31:0] R2_Out,
  output MemWeite_Out,
  output [3:0] ALUop_Out,
  output [4:0] RegW__Out,
  output [31:0] JMP_addr,
  output RegWB_2,
  output [1:0] RF_Din_Out,
  output SysCall_Out,
  output Branch
);

  wire and_3_out, and_4_out, not_1_out, or_1_out, or_4_out;
  wire [1:0] ALUsrc_t;
  wire [4:0] shmat_t;
  wire [15:0] IMM_t;
  wire [16:13] register_9_q;
  wire [17:0] multiplexer_9_out;
  wire [25:0] Addr_t;
  wire [31:0] adder_1_out, adder_2_out, adder_3_out, and_1_out, and_2_out, bit_extender_1_out,
       bit_extender_2_out, bit_extender_3_out, bit_extender_4_out, Instr_In_t, multiplexer_10_out,
       multiplexer_11_out, multiplexer_12_out, multiplexer_13_out, or_2_out, PC_In_t, R1_t, R2_t,
       register_3_q, register_7_q, register_8_q, shifter_1_out, shifter_2_out;

  Multiplexer #(.width(26), .disabled(0), .enable("false")) multiplexer_1 (
    .in0(Addr), .in1({26{1'b0}}), .out(Addr_t), .sel(or_1_out));
  Multiplexer #(.width(32), .disabled(0), .enable("false")) multiplexer_2 (
    .in0(PC_In), .in1({32{1'b0}}), .out(PC_In_t), .sel(or_1_out));
  Multiplexer #(.width(32), .disabled(0), .enable("false")) multiplexer_3 (
    .in0(Instr_In), .in1({32{1'b0}}), .out(Instr_In_t), .sel(or_1_out));
  Multiplexer #(.width(32), .disabled(0), .enable("false")) multiplexer_4 (
    .in0(R1), .in1({32{1'b0}}), .out(R1_t), .sel(or_1_out));
  Multiplexer #(.width(32), .disabled(0), .enable("false")) multiplexer_5 (
    .in0(R2), .in1({32{1'b0}}), .out(R2_t), .sel(or_1_out));
  Multiplexer #(.width(16), .disabled(0), .enable("false")) multiplexer_6 (
    .in0(IMM), .in1({16{1'b0}}), .out(IMM_t), .sel(or_1_out));
  Multiplexer #(.width(5), .disabled(0), .enable("false")) multiplexer_7 (
    .in0(shmat), .in1({5{1'b0}}), .out(shmat_t), .sel(or_1_out));
  Multiplexer #(.width(2), .disabled(0), .enable("false")) multiplexer_8 (
    .in0(ALUsrc), .in1(2'b00), .out(ALUsrc_t), .sel(or_1_out));
  Multiplexer #(.width(18), .disabled(0), .enable("false")) multiplexer_9 (
    .in0({SysCall, BEQ, BNE, PcControl, RF_Din, RegWB, RegW_num, ALUop, MemWrite}), .in1({18{1'b0}}),
    .out(multiplexer_9_out), .sel(or_1_out));
  or or_1 (or_1_out, B_Clr, C_Clr);
  assign bit_extender_1_out = {{16{IMM_t[15]}}, IMM_t};  // Bit_Extender bit_extender_1
  assign bit_extender_2_out = {{16{1'b0}}, IMM_t};  // Bit_Extender bit_extender_2
  assign bit_extender_3_out = {{27{1'b0}}, shmat_t};  // Bit_Extender bit_extender_3
  Adder #(.width(32)) adder_1 (.a(PC_In_t), .b(32'h4), .out(adder_1_out));  // open: cin, cout
  assign bit_extender_4_out = {{6{Addr_t[25]}}, Addr_t};  // Bit_Extender bit_extender_4
  assign and_1_out = adder_1_out & 32'hf0000000;  // AND_Gate and_1, 32 bits wide
  Shifter #(.width(32)) shifter_1 (.in(bit_extender_4_out), .\dist (5'b00010), .out(shifter_1_out));
  Shifter #(.width(32)) shifter_2 (.in(bit_extender_1_out), .\dist (5'b00010), .out(shifter_2_out));
  Multiplexer #(.select(2), .width(32), .enable("false")) multiplexer_10 (
    .in0(R2_t), .in1(bit_extender_1_out), .in2(bit_extender_2_out), .in3(bit_extender_3_out),
    .out(multiplexer_10_out), .sel(ALUsrc_t));
  assign or_2_out = and_1_out | shifter_1_out;  // OR_Gate or_2, 32 bits wide
  assign and_2_out = or_2_out & 32'hfff;  // AND_Gate and_2, 32 bits wide
  Multiplexer #(.width(32), .enable("false")) multiplexer_11 (
    .in0(R1_t), .in1(PC_In_t), .out(multiplexer_11_out), .sel(JAL));
  Multiplexer #(.width(32), .enable("false")) multiplexer_12 (
    .in0(multiplexer_10_out), .in1(32'h4), .out(multiplexer_12_out), .sel(JAL));
  Register #(.width(32)) register_1 (.D(Instr_In_t), .Q(Instr_Out), .clk(in_1));  // open: en, clr
  Register #(.width(32)) register_2 (.D(PC_In_t), .Q(PC_Out), .clk(in_1));  // open: en, clr
  Register #(.width(32)) register_3 (.D(shifter_2_out), .Q(register_3_q), .clk(in_1));  // open: en, clr
  Register #(.width(32)) register_4 (.D(multiplexer_11_out), .Q(X), .clk(in_1));  // open: en, clr
  Register #(.width(32)) register_5 (.D(multiplexer_12_out), .Q(Y), .clk(in_1));  // open: en, clr
  Register #(.width(32)) register_6 (.D(R2_t), .Q(R2_Out), .clk(in_1));  // open: en, clr
  Register #(.width(32)) register_7 (.D(R1_t), .Q(register_7_q), .clk(in_1));  // open: en, clr
  Register #(.width(32)) register_8 (.D(and_2_out), .Q(register_8_q), .clk(in_1));  // open: en, clr
  Register #(.width(18)) register_9 (
    .D(multiplexer_9_out),
    .Q({SysCall_Out, register_9_q, RF_Din_Out, RegWB_2, RegW__Out, ALUop_Out, MemWeite_Out}), .clk(in_1));  // open: en, clr
  or or_3 (Branch, register_9_q[14], or_4_out);
  Adder #(.width(32)) adder_2 (.a(32'h4), .b(PC_Out), .out(adder_2_out));  // open: cin, cout
  not not_1 (not_1_out, EQUAL);
  and and_3 (and_3_out, not_1_out, register_9_q[15]);
  and and_4 (and_4_out, EQUAL, register_9_q[16]);
  Multiplexer #(.width(32), .enable("false")) multiplexer_13 (
    .in0({32{1'b0}}), .in1(register_3_q), .out(multiplexer_13_out), .sel(or_4_out));
  or or_4 (or_4_out, and_3_out, and_4_out);
  Adder #(.width(32)) adder_3 (.a(adder_2_out), .b(multiplexer_13_out), .out(adder_3_out));  // open: cin, cout
  Multiplexer #(.select(2), .width(32), .enable("false")) multiplexer_14 (
    .in0(adder_2_out), .in1(adder_3_out), .in2(register_8_q), .in3(register_7_q), .out(JMP_addr),
    .sel(register_9_q[14:13]));

  // Other names for the same wires on the sheet: Clk = in_1
endmodule

module EX_MEM (
  input  in_1,
  input  [31:0] Instr_In,
  input  [31:0] PC_In,
  input  [31:0] Addr,
  input  [31:0] DM_Din,
  input  MemWrite,
  input  [31:0] LO_In,
  input  [1:0] RF_Din,
  input  [31:0] HI_In,
  input  RegWB,
  input  [4:0] RegW_num,
  input  SysCall,
  output [31:0] Instr_Out,
  output [31:0] PC_Out,
  output [31:0] Reg_Data,
  output [23:0] Addr_2,
  output [31:0] DM_Din_2,
  output [31:0] HI_Out,
  output [31:0] LO_Out,
  output MemWriteEn,
  output [1:0] RF_Din_2,
  output RegWB_2,
  output [4:0] RegW_num_2,
  output SysCall_Out
);

  Register #(.width(32)) register_1 (.D(Instr_In), .Q(Instr_Out), .clk(in_1));  // open: en, clr
  Register #(.width(32)) register_2 (.D(PC_In), .Q(PC_Out), .clk(in_1));  // open: en, clr
  Register #(.width(32)) register_3 (
    .D(Addr), .Q({Reg_Data[31:26], Addr_2, Reg_Data[1:0]}), .clk(in_1));  // open: en, clr
  Register #(.width(32)) register_4 (.D(DM_Din), .Q(DM_Din_2), .clk(in_1));  // open: en, clr
  Register #(.width(32)) register_5 (.D(HI_In), .Q(HI_Out), .clk(in_1));  // open: en, clr
  Register #(.width(32)) register_6 (.D(LO_In), .Q(LO_Out), .clk(in_1));  // open: en, clr
  Register #(.width(10)) register_7 (
    .D({SysCall, RegW_num, RegWB, RF_Din, MemWrite}),
    .Q({SysCall_Out, RegW_num_2, RegWB_2, RF_Din_2, MemWriteEn}), .clk(in_1));  // open: en, clr

  assign Reg_Data[25:2] = Addr_2;

  // Other names for the same wires on the sheet: Clk = in_1
endmodule

module MEM_WB (
  input  Clk,
  input  [31:0] LO_In,
  input  [31:0] Instr_In,
  input  [1:0] RF_Din,
  input  [31:0] HI_In,
  input  [31:0] PC_In,
  input  [31:0] Reg_Data,
  input  [31:0] DM_Out,
  input  SysCall,
  input  RegWB,
  input  [4:0] RegW_num,
  output [31:0] Instr_Out,
  output [31:0] PC_Out,
  output [31:0] WB_data,
  output RegWB_2,
  output [4:0] RegW_num_2,
  output SYSCALL_2
);

  wire [31:0] multiplexer_1_out;

  Register #(.width(32)) register_1 (.D(Instr_In), .Q(Instr_Out), .clk(Clk));  // open: en, clr
  Register #(.width(32)) register_2 (.D(PC_In), .Q(PC_Out), .clk(Clk));  // open: en, clr
  Multiplexer #(.select(2), .width(32), .enable("false")) multiplexer_1 (
    .in0(Reg_Data), .in1(DM_Out), .in2(HI_In), .in3(LO_In), .out(multiplexer_1_out), .sel(RF_Din));
  Register #(.width(32)) register_3 (.D(multiplexer_1_out), .Q(WB_data), .clk(Clk));  // open: en, clr
  Register #(.width(7)) register_4 (
    .D({SysCall, RegW_num, RegWB}), .Q({SYSCALL_2, RegW_num_2, RegWB_2}), .clk(Clk));  // open: en, clr
endmodule

module ConflictUnit (
  input  Branch,
  input  [31:0] EX_Instr,
  input  [31:0] MEM_Instr,
  input  [4:0] R1,
  input  [4:0] R2,
  input  EX_RWB,
  input  [4:0] EX_RW_num,
  input  MEM_RWB,
  input  [4:0] MEM_RW_num,
  output IF_ID_Clr,
  output Jmp,
  output B_ID_EX_Clr,
  output Stop_Clk,
  output C_ID_EX_Clr,
  output Conflict
);

  wire and_1_out, and_2_out, and_3_out, and_4_out, comparator_1_eq, comparator_2_eq, comparator_3_eq,
       comparator_4_eq, comparator_5_eq, comparator_6_eq, not_1_out, not_2_out, not_3_out, or_1_out,
       or_2_out, or_3_out;

  Comparator #(.width(5)) comparator_1 (.a(R1), .b(EX_RW_num), .eq(comparator_1_eq));  // open: gt, lt
  Comparator #(.width(5)) comparator_2 (.a(R2), .b(EX_RW_num), .eq(comparator_2_eq));  // open: gt, lt
  Comparator #(.width(5)) comparator_3 (.a(R1), .b(MEM_RW_num), .eq(comparator_3_eq));  // open: gt, lt
  Comparator #(.width(5)) comparator_4 (.a(R2), .b(MEM_RW_num), .eq(comparator_4_eq));  // open: gt, lt
  or or_1 (or_1_out, comparator_1_eq, comparator_2_eq);
  or or_2 (or_2_out, comparator_3_eq, comparator_4_eq);
  and and_1 (and_1_out, EX_RWB, or_1_out);
  Comparator #(.width(32)) comparator_5 (.a(EX_Instr), .b({32{1'b0}}), .eq(comparator_5_eq));  // open: gt, lt
  and and_2 (and_2_out, MEM_RWB, or_2_out);
  Comparator #(.width(32)) comparator_6 (.a(MEM_Instr), .b({32{1'b0}}), .eq(comparator_6_eq));  // open: gt, lt
  not not_1 (not_1_out, comparator_5_eq);
  not not_2 (not_2_out, comparator_6_eq);
  and and_3 (and_3_out, and_1_out, not_1_out);
  and and_4 (and_4_out, and_2_out, not_2_out);
  or or_3 (or_3_out, and_3_out, and_4_out);
  and and_5 (C_ID_EX_Clr, or_3_out, not_3_out);
  not not_3 (not_3_out, Branch);

  assign B_ID_EX_Clr = Branch;
  assign Conflict = C_ID_EX_Clr;
  assign IF_ID_Clr = Branch;
  assign Jmp = Branch;
  assign Stop_Clk = C_ID_EX_Clr;
endmodule
