// Logisim project Flows_Bypass.circ as structural Verilog: 10 circuits, main circuit main
module main (
  input  [4:0] in_1
);

  wire alu_1_equal, and_1_out, btb_1_forecast_jmp, Clk, clock_1_out, comparator_1_eq, comparator_2_eq,
       conflictunit_1_conflict, conflictunit_1_id_ex_clr, conflictunit_1_if_id_clr, conflictunit_1_jmp,
       conflictunit_1_pc_ch, conflictunit_1_r1_ch, conflictunit_1_r2_ch, conflictunit_1_stop_clk,
       controlunit_1_beq, controlunit_1_bne, controlunit_1_jal, controlunit_1_memwrite, controlunit_1_r1_num,
       controlunit_1_regwirteback, controlunit_1_syscall, ex_mem_1_memwriteen, ex_mem_1_regwb_2,
       ex_mem_1_syscall_out, hilocontrol_1_hilocontrol, id_ex_1_error, id_ex_1_jmp, id_ex_1_memweite_out,
       id_ex_1_regwb_2, id_ex_1_syscall_out, if_id_1_forecast_2, mem_wb_1_regwb_2, not_1_out, not_2_out,
       not_3_out, not_4_out, not_5_out, SysCall;
  wire [1:0] controlunit_1_alusrc, controlunit_1_pccontrol, controlunit_1_rf_din, controlunit_1_w_num,
       ex_mem_1_rf_din_2, id_ex_1_rf_din_out;
  wire [3:0] controlunit_1_aluop, id_ex_1_aluop_out, register_2_q_2, register_2_q_3, register_2_q_4,
       register_2_q_5;
  wire [4:0] ex_mem_1_regw_num_2, id_ex_1_regw__out, instrdecode_1_rd, instrdecode_1_rs, instrdecode_1_rt,
       instrdecode_1_shamt, mem_wb_1_regw_num_2, multiplexer_4_out, multiplexer_5_out;
  wire [5:0] instrdecode_1_funct, instrdecode_1_opcode;
  wire [15:0] instrdecode_1_imm, register_2_q;
  wire [23:0] ex_mem_1_addr_2, if_id_1_pc_out_2;
  wire [25:0] instrdecode_1_addr;
  wire [31:0] a0, alu_1_result, alu_1_result_2, btb_1_pc_out, conflictunit_1_r1_d_out,
       conflictunit_1_r2_d_out, counter_1_q, counter_2_q, counter_3_q, DebugValue, ex_mem_1_dm_din_2,
       ex_mem_1_ex_reg_data, ex_mem_1_hi_out, ex_mem_1_instr_out, ex_mem_1_lo_out, ex_mem_1_pc_out,
       ex_mem_1_reg_data, hilo_1_hi_out, hilo_1_lo_out, id_ex_1_back_instr, id_ex_1_back_pc,
       id_ex_1_branch_pc, id_ex_1_instr_out, id_ex_1_jmp_addr, id_ex_1_pc_out, id_ex_1_r2_out, id_ex_1_x,
       id_ex_1_y, if_id_1_instr, if_id_1_instr_out, if_id_1_pc_out, mem_wb_1_instr_out,
       mem_wb_1_mem_reg_data, mem_wb_1_pc_out, mem_wb_1_wb_data, multiplexer_1_out, multiplexer_3_out,
       multiplexer_6_out, multiplexer_7_out, ram_1_data, regfile_1_reg1, regfile_1_reg2_2, register_1_q,
       rom_1_data, v0;

  Register #(.width(32)) register_1 (
    .D(multiplexer_1_out), .en(conflictunit_1_stop_clk), .Q(register_1_q), .clk(Clk));  // open: clr
  Multiplexer #(.width(32), .enable("false")) multiplexer_1 (
    .in0(btb_1_pc_out), .in1(id_ex_1_jmp_addr), .out(multiplexer_1_out), .sel(conflictunit_1_pc_ch));
  ConflictUnit conflictunit_1 (
    .Branch(id_ex_1_error), .IF_ID_Clr(conflictunit_1_if_id_clr), .R1(multiplexer_4_out),
    .R2(instrdecode_1_rt), .EX_RWB(id_ex_1_regwb_2), .EX_RW_num(id_ex_1_regw__out),
    .MEM_RWB(ex_mem_1_regwb_2), .MEM_RW_num(ex_mem_1_regw_num_2), .ID_EX_Clr(conflictunit_1_id_ex_clr),
    .EX_Instr(id_ex_1_instr_out), .MEM_Instr(ex_mem_1_instr_out), .Jmp(conflictunit_1_jmp),
    .MEM_Reg_Data(mem_wb_1_mem_reg_data), .R1_D_Out(conflictunit_1_r1_d_out), .R1_Ch(conflictunit_1_r1_ch),
    .Stop_Clk(conflictunit_1_stop_clk), .EX_Reg_Data(ex_mem_1_ex_reg_data),
    .R2_D_Out(conflictunit_1_r2_d_out), .R2_Ch(conflictunit_1_r2_ch), .Conflict(conflictunit_1_conflict),
    .Pc_ch(conflictunit_1_pc_ch));
  BTB btb_1 (
    .Pc_In(register_1_q), .Pc_Out(btb_1_pc_out), .Back_pc(id_ex_1_back_pc), .Clk(Clk),
    .Branch_pc(id_ex_1_branch_pc), .Current_Instr(rom_1_data), .Forecast_Jmp(btb_1_forecast_jmp),
    .Success(id_ex_1_jmp), .Back_Instr(id_ex_1_back_instr));
  // Probe on register_1_q[25:2]
  ROM #(.addrWidth(24), .dataWidth(32)) rom_1 (.addr(register_1_q[25:2]), .data(rom_1_data));  // open: sel
  // Probe on DebugValue
  Comparator #(.width(32)) comparator_1 (.a(v0), .b(32'ha), .eq(comparator_1_eq));  // open: gt, lt
  and and_1 (and_1_out, comparator_1_eq, SysCall);
  Clock clock_1 (.out(clock_1_out));
  // Probe on rom_1_data
  IF_ID if_id_1 (
    .Clk(Clk), .Code(rom_1_data), .Instr_Out(if_id_1_instr_out), .Instr(if_id_1_instr), .PC_In(register_1_q),
    .PC_Out({if_id_1_pc_out[31:26], if_id_1_pc_out_2, if_id_1_pc_out[1:0]}), .Clr(conflictunit_1_if_id_clr),
    .Stop_Clk(conflictunit_1_stop_clk), .Forecast(btb_1_forecast_jmp), .Forecast_2(if_id_1_forecast_2));
  // Probe on in_1
  Hex_Digit_Display hex_digit_display_1 (.value(register_2_q_5));  // open: dp
  Multiplexer #(.enable("false")) multiplexer_2 (.in0(clock_1_out), .in1(1'b0), .out(Clk), .sel(and_1_out));
  // Probe on if_id_1_pc_out_2
  // Probe on if_id_1_instr
  InstrDecode instrdecode_1 (
    .rd(instrdecode_1_rd), .rt(instrdecode_1_rt), .Addr(instrdecode_1_addr), .IMM(instrdecode_1_imm),
    .IND(if_id_1_instr_out), .rs(instrdecode_1_rs), .Funct(instrdecode_1_funct),
    .OpCode(instrdecode_1_opcode), .shamt(instrdecode_1_shamt));
  Hex_Digit_Display hex_digit_display_2 (.value(register_2_q_4));  // open: dp
  Hex_Digit_Display hex_digit_display_3 (.value(register_2_q_3));  // open: dp
  Multiplexer #(.width(32), .enable("false")) multiplexer_3 (
    .in1(a0), .out(multiplexer_3_out), .sel(not_1_out));  // open: in0
  not not_1 (not_1_out, and_1_out);
  Hex_Digit_Display hex_digit_display_4 (.value(register_2_q[15:12]));  // open: dp
  Hex_Digit_Display hex_digit_display_5 (.value(register_2_q_2));  // open: dp
  Register #(.width(32)) register_2 (
    .D(multiplexer_3_out),
    .Q({register_2_q_5, register_2_q_4, register_2_q_3, register_2_q_2, register_2_q}), .clk(Clk));  // open: en, clr
  Multiplexer #(.width(5), .enable("false")) multiplexer_4 (
    .in0(instrdecode_1_rs), .in1(instrdecode_1_rt), .out(multiplexer_4_out), .sel(controlunit_1_r1_num));
  Multiplexer #(.select(2), .width(5), .enable("false")) multiplexer_5 (
    .in0(instrdecode_1_rt), .in1({5{1'b1}}), .in2(instrdecode_1_rd), .out(multiplexer_5_out),
    .sel(controlunit_1_w_num));  // open: in3
  ControlUnit controlunit_1 (
    .RegWirteBack(controlunit_1_regwirteback), .ALUop(controlunit_1_aluop),
    .PcControl(controlunit_1_pccontrol), .W_num(controlunit_1_w_num), .R1_num(controlunit_1_r1_num),
    .RF_Din(controlunit_1_rf_din), .MemWrite(controlunit_1_memwrite), .ALUsrc(controlunit_1_alusrc),
    .SysCall(controlunit_1_syscall), .BNE(controlunit_1_bne), .BEQ(controlunit_1_beq),
    .JAl(controlunit_1_jal), .OpCode(instrdecode_1_opcode), .Funct(instrdecode_1_funct));
  Hex_Digit_Display hex_digit_display_6 (.value(register_2_q[7:4]));  // open: dp
  Hex_Digit_Display hex_digit_display_7 (.value(register_2_q[11:8]));  // open: dp
  Hex_Digit_Display hex_digit_display_8 (.value(register_2_q[3:0]));  // open: dp
  not not_2 (not_2_out, comparator_2_eq);
  RegFile regfile_1 (
    .Reg1_num(multiplexer_4_out), .Reg2(instrdecode_1_rt), .Write_Reg_num(mem_wb_1_regw_num_2),
    .Din(mem_wb_1_wb_data), .Write_Enable(mem_wb_1_regwb_2), .Clock(not_3_out), .Reg1(regfile_1_reg1),
    .Reg2_2(regfile_1_reg2_2), .v0(v0), .a0(a0), .in_3(in_1), .DebugValue(DebugValue));
  not not_3 (not_3_out, Clk);
  // Probe on counter_1_q
  Counter #(.width(32), .max('hffffffff), .trigger("falling")) counter_1 (
    .load(comparator_2_eq), .D(32'h2), .count(not_2_out), .Q(counter_1_q), .clk(Clk));  // open: carry, clr
  Multiplexer #(.width(32), .enable("false")) multiplexer_6 (
    .in0(regfile_1_reg1), .in1(conflictunit_1_r1_d_out), .out(multiplexer_6_out), .sel(conflictunit_1_r1_ch));
  Multiplexer #(.width(32), .enable("false")) multiplexer_7 (
    .in0(regfile_1_reg2_2), .in1(conflictunit_1_r2_d_out), .out(multiplexer_7_out), .sel(conflictunit_1_r2_ch));
  Comparator #(.width(32)) comparator_2 (.a(counter_1_q), .b({32{1'b0}}), .eq(comparator_2_eq));  // open: gt, lt
  // Probe on id_ex_1_pc_out[25:2]
  ID_EX id_ex_1 (
    .in_1(Clk), .Instr_In(if_id_1_instr), .Instr_Out(id_ex_1_instr_out), .R1(multiplexer_6_out),
    .R2(multiplexer_7_out), .PC_In({if_id_1_pc_out[31:26], if_id_1_pc_out_2, if_id_1_pc_out[1:0]}),
    .PC_Out(id_ex_1_pc_out), .shmat(instrdecode_1_shamt), .IMM(instrdecode_1_imm), .JAL(controlunit_1_jal),
    .ALUsrc(controlunit_1_alusrc), .X(id_ex_1_x), .Y(id_ex_1_y), .ALUop(controlunit_1_aluop),
    .Addr(instrdecode_1_addr), .RegW_num(multiplexer_5_out), .RegWB(controlunit_1_regwirteback),
    .RF_Din(controlunit_1_rf_din), .MemWrite(controlunit_1_memwrite), .MemWeite_Out(id_ex_1_memweite_out),
    .ALUop_Out(id_ex_1_aluop_out), .RegW__Out(id_ex_1_regw__out), .RegWB_2(id_ex_1_regwb_2),
    .RF_Din_Out(id_ex_1_rf_din_out), .PcControl(controlunit_1_pccontrol), .BNE(controlunit_1_bne),
    .BEQ(controlunit_1_beq), .R2_Out(id_ex_1_r2_out), .EQUAL(alu_1_equal), .JMP_addr(id_ex_1_jmp_addr),
    .SysCall(controlunit_1_syscall), .SysCall_Out(id_ex_1_syscall_out), .Clr(conflictunit_1_id_ex_clr),
    .Back_pc(id_ex_1_back_pc), .Branch_pc(id_ex_1_branch_pc), .forecast(if_id_1_forecast_2),
    .Back_Instr(id_ex_1_back_instr), .error(id_ex_1_error), .Jmp(id_ex_1_jmp));
  // Probe on counter_2_q
  Counter #(.width(32), .max('hffffffff)) counter_2 (
    .count(conflictunit_1_jmp), .Q(counter_2_q), .clk(Clk));  // open: load, D, carry, clr
  // Probe on counter_3_q
  Counter #(.width(32), .max('hffffffff)) counter_3 (
    .count(conflictunit_1_conflict), .Q(counter_3_q), .clk(Clk));  // open: load, D, carry, clr
  // Probe on id_ex_1_instr_out
  ALU alu_1 (
    .AluOP(id_ex_1_aluop_out), .X(id_ex_1_x), .Equal(alu_1_equal), .Result(alu_1_result), .Y(id_ex_1_y),
    .Result_2(alu_1_result_2));  // open: Signed_Overflow, UnSigned_Overflow
  HILO hilo_1 (
    .HI_In(alu_1_result_2), .LO_In(alu_1_result), .Clk(not_4_out), .Control(hilocontrol_1_hilocontrol),
    .HI_Out(hilo_1_hi_out), .LO_Out(hilo_1_lo_out));
  HILOControl hilocontrol_1 (.ALUop(id_ex_1_aluop_out), .HILOControl(hilocontrol_1_hilocontrol));
  not not_4 (not_4_out, Clk);
  EX_MEM ex_mem_1 (
    .in_1(Clk), .Instr_In(id_ex_1_instr_out), .PC_In(id_ex_1_pc_out), .Instr_Out(ex_mem_1_instr_out),
    .PC_Out(ex_mem_1_pc_out), .Addr(alu_1_result), .Reg_Data(ex_mem_1_reg_data), .Addr_2(ex_mem_1_addr_2),
    .DM_Din(id_ex_1_r2_out), .DM_Din_2(ex_mem_1_dm_din_2), .MemWrite(id_ex_1_memweite_out),
    .MemWriteEn(ex_mem_1_memwriteen), .RF_Din(id_ex_1_rf_din_out), .RF_Din_2(ex_mem_1_rf_din_2),
    .LO_In(hilo_1_lo_out), .HI_In(hilo_1_hi_out), .HI_Out(ex_mem_1_hi_out), .LO_Out(ex_mem_1_lo_out),
    .RegW_num(id_ex_1_regw__out), .RegWB(id_ex_1_regwb_2), .RegWB_2(ex_mem_1_regwb_2),
    .RegW_num_2(ex_mem_1_regw_num_2), .SysCall(id_ex_1_syscall_out), .SysCall_Out(ex_mem_1_syscall_out),
    .EX_Reg_Data(ex_mem_1_ex_reg_data));
  // Probe on ex_mem_1_pc_out[25:2]
  // Probe on ex_mem_1_instr_out
  not not_5 (not_5_out, Clk);
  RAM #(.addrWidth(24), .dataWidth(32), .bus("separate")) ram_1 (
    .addr(ex_mem_1_addr_2), .din(ex_mem_1_dm_din_2), .data(ram_1_data), .str(ex_mem_1_memwriteen),
    .clk(not_5_out), .ld(ex_mem_1_rf_din_2[0]));  // open: sel, clr
  MEM_WB mem_wb_1 (
    .LO_In(ex_mem_1_lo_out), .HI_In(ex_mem_1_hi_out), .Clk(Clk), .Reg_Data(ex_mem_1_reg_data),
    .DM_Out(ram_1_data), .RF_Din(ex_mem_1_rf_din_2), .WB_data(mem_wb_1_wb_data), .RegWB(ex_mem_1_regwb_2),
    .RegW_num(ex_mem_1_regw_num_2), .RegWB_2(mem_wb_1_regwb_2), .RegW_num_2(mem_wb_1_regw_num_2),
    .Instr_Out(mem_wb_1_instr_out), .PC_Out(mem_wb_1_pc_out), .Instr_In(ex_mem_1_instr_out),
    .PC_In(ex_mem_1_pc_out), .SysCall(ex_mem_1_syscall_out), .SYSCALL_2(SysCall),
    .MEM_Reg_Data(mem_wb_1_mem_reg_data));
  // Probe on mem_wb_1_pc_out[25:2]
  // Probe on mem_wb_1_instr_out

  // Other names for the same wires on the sheet: Debug[4:0] = in_1

  // Notes on the sheet:
  //   contents of rom_1 (hex, n*v repeats v):
  //   20110001 8000c05 20110001 20120002 20130003 8000c09 20110001 20120002 20130003 8000c0d 20110001
  //   20120002 20130003 8000c11 20110001 20120002 20130003 c000cce 20110001 20120010 112020 20020022 c
  //   2320018 4810 8812 112020 20020022 c 1120fff9 20110001 20120010 118fc0 112020 20020022 c 232001b 4810
  //   8812 1620fff9 20100001 20110001 118fc0 112020 20020022 c 118882 12200001 8000c2b 112020 20020022 c
  //   20110001 118880 112020 20020022 c 12200001 8000c35 20110001 118fc0 112020 20020022 c 1188c3 112020
  //   20020022 c 118903 112020 20020022 c 118903 112020 20020022 c 118903 112020 20020022 c 118903 112020
  //   20020022 c 118903 112020 20020022 c 118903 112020 20020022 c 118903 112020 20020022 c 20100001
  //   109fc0 139fc3 8021 2012000c 24160003 26100001 3210000f 20080008 20090001 139900 2709825 132020
  //   20020022 c 1094022 1500fff9 22100001 2018000f 2188024 108700 20080008 20090001 139902 2709825 132021
  //   20020022 c 1094022 1500fff9 108702 2c9b022 12c00001 8000c66 4020 1084027 84400 3508ffff 82021
  //   20020022 c 2010ffff 20110000 ae300000 22100001 22310004 ae300000 22100001 22310004 ae300000 22100001
  //   22310004 ae300000 22100001 22310004 ae300000 22100001 22310004 ae300000 22100001 22310004 ae300000
  //   22100001 22310004 ae300000 22100001 22310004 ae300000 22100001 22310004 ae300000 22100001 22310004
  //   ae300000 22100001 22310004 ae300000 22100001 22310004 ae300000 22100001 22310004 ae300000 22100001
  //   22310004 ae300000 22100001 22310004 ae300000 22100001 22310004 22100001 8020 2011003c 8e130000
  //   8e340000 274402a 11000002 ae330000 ae140000 2231fffc 1611fff8 102020 20020022 c 22100004 2011003c
  //   1611fff2 2002000a c 20100000 22100001 102020 20020022 c 22100002 102020 20020022 c 22100003 102020
  //   20020022 c 22100004 102020 20020022 c 22100005 102020 20020022 c 22100006 102020 20020022 c 22100007
  //   102020 20020022 c 22100008 102020 20020022 20020022 c 3e00008
endmodule

module IF_ID (
  input  Clk,
  input  Clr,
  input  Stop_Clk,
  input  [31:0] Code,
  input  [31:0] PC_In,
  input  Forecast,
  output [31:0] Instr_Out,
  output [31:0] Instr,
  output [31:0] PC_Out,
  output Forecast_2
);

  wire multiplexer_3_out;
  wire [31:0] multiplexer_1_out, multiplexer_2_out;

  // Probe on Code
  // Probe on PC_In
  Multiplexer #(.width(32), .enable("false")) multiplexer_1 (
    .in0(Code), .in1({32{1'b0}}), .out(multiplexer_1_out), .sel(Clr));
  Multiplexer #(.width(32), .enable("false")) multiplexer_2 (
    .in0(PC_In), .in1({32{1'b0}}), .out(multiplexer_2_out), .sel(Clr));
  Multiplexer #(.enable("false")) multiplexer_3 (.in0(Forecast), .in1(1'b0), .out(multiplexer_3_out), .sel(Clr));
  Register #(.width(32)) register_1 (.D(multiplexer_1_out), .en(Stop_Clk), .Q(Instr), .clk(Clk));  // open: clr
  Register #(.width(32)) register_2 (.D(multiplexer_2_out), .en(Stop_Clk), .Q(PC_Out), .clk(Clk));  // open: clr
  Register #(.width(1)) register_3 (.D(multiplexer_3_out), .en(Stop_Clk), .Q(Forecast_2), .clk(Clk));  // open: clr

  assign Instr_Out = Instr;
endmodule

module ID_EX (
  input  in_1,
  input  JAL,
  input  Clr,
  input  [3:0] ALUop,
  input  MemWrite,
  input  EQUAL,
  input  [1:0] PcControl,
  input  BNE,
  input  BEQ,
  input  RegWB,
  input  SysCall,
  input  [4:0] RegW_num,
  input  [1:0] RF_Din,
  input  [25:0] Addr,
  input  [31:0] PC_In,
  input  [31:0] Instr_In,
  input  [31:0] R1,
  input  [31:0] R2,
  input  [15:0] IMM,
  input  [4:0] shmat,
  input  [1:0] ALUsrc,
  input  forecast,
  output [31:0] Back_Instr,
  output [31:0] Branch_pc,
  output [31:0] Back_pc,
  output [31:0] Instr_Out,
  output [31:0] PC_Out,
  output [31:0] X,
  output [31:0] Y,
  output [31:0] R2_Out,
  output MemWeite_Out,
  output [3:0] ALUop_Out,
  output [4:0] RegW__Out,
  output [31:0] JMP_addr,
  output RegWB_2,
  output [1:0] RF_Din_Out,
  output SysCall_Out,
  output Jmp,
  output error
);

  wire and_3_out, and_4_out, and_6_out, and_7_out, forecast_t, Is_branch, not_1_out, not_2_out, not_3_out,
       not_4_out, or_3_out, or_4_out, register_10_q;
  wire [1:0] ALUsrc_t;
  wire [4:0] shmat_t;
  wire [15:0] IMM_t;
  wire [16:13] register_9_q;
  wire [17:0] multiplexer_9_out;
  wire [25:0] Addr_t;
  wire [31:0] adder_1_out, adder_2_out, adder_3_out, and_1_out, and_2_out, bit_extender_1_out,
       bit_extender_2_out, bit_extender_3_out, bit_extender_4_out, Instr_In_t, multiplexer_11_out,
       multiplexer_12_out, multiplexer_13_out, multiplexer_17_out, or_1_out, PC_In_t, R1_t, R2_t,
       register_3_q, register_7_q, register_8_q, shifter_1_out, shifter_2_out;

  Multiplexer #(.width(26), .disabled(0), .enable("false")) multiplexer_1 (
    .in0(Addr), .in1({26{1'b0}}), .out(Addr_t), .sel(Clr));
  Multiplexer #(.width(32), .disabled(0), .enable("false")) multiplexer_2 (
    .in0(PC_In), .in1({32{1'b0}}), .out(PC_In_t), .sel(Clr));
  Multiplexer #(.width(32), .disabled(0), .enable("false")) multiplexer_3 (
    .in0(Instr_In), .in1({32{1'b0}}), .out(Instr_In_t), .sel(Clr));
  Multiplexer #(.width(32), .disabled(0), .enable("false")) multiplexer_4 (
    .in0(R1), .in1({32{1'b0}}), .out(R1_t), .sel(Clr));
  Multiplexer #(.width(32), .disabled(0), .enable("false")) multiplexer_5 (
    .in0(R2), .in1({32{1'b0}}), .out(R2_t), .sel(Clr));
  Multiplexer #(.width(16), .disabled(0), .enable("false")) multiplexer_6 (
    .in0(IMM), .in1({16{1'b0}}), .out(IMM_t), .sel(Clr));
  Multiplexer #(.width(5), .disabled(0), .enable("false")) multiplexer_7 (
    .in0(shmat), .in1({5{1'b0}}), .out(shmat_t), .sel(Clr));
  Multiplexer #(.width(2), .disabled(0), .enable("false")) multiplexer_8 (
    .in0(ALUsrc), .in1(2'b00), .out(ALUsrc_t), .sel(Clr));
  Multiplexer #(.width(18), .disabled(0), .enable("false")) multiplexer_9 (
    .in0({SysCall, BEQ, BNE, PcControl, RF_Din, RegWB, RegW_num, ALUop, MemWrite}), .in1({18{1'b0}}),
    .out(multiplexer_9_out), .sel(Clr));
  Multiplexer #(.enable("false")) multiplexer_10 (.in0(forecast), .in1(1'b0), .out(forecast_t), .sel(Clr));
  assign bit_extender_1_out = {{16{IMM_t[15]}}, IMM_t};  // Bit_Extender bit_extender_1
  assign bit_extender_2_out = {{16{1'b0}}, IMM_t};  // Bit_Extender bit_extender_2
  assign bit_extender_3_out = {{27{1'b0}}, shmat_t};  // Bit_Extender bit_extender_3
  Adder #(.width(32)) adder_1 (.a(PC_In_t), .b(32'h4), .out(adder_1_out));  // open: cin, cout
  assign bit_extender_4_out = {{6{Addr_t[25]}}, Addr_t};  // Bit_Extender bit_extender_4
  assign and_1_out = adder_1_out & 32'hf0000000;  // AND_Gate and_1, 32 bits wide
  Shifter #(.width(32)) shifter_1 (.in(bit_extender_4_out), .\dist (5'b00010), .out(shifter_1_out));
  Shifter #(.width(32)) shifter_2 (.in(bit_extender_1_out), .\dist (5'b00010), .out(shifter_2_out));
  Multiplexer #(.select(2), .width(32), .enable("false")) multiplexer_11 (
    .in0(R2_t), .in1(bit_extender_1_out), .in2(bit_extender_2_out), .in3(bit_extender_3_out),
    .out(multiplexer_11_out), .sel(ALUsrc_t));
  assign or_1_out = and_1_out | shifter_1_out;  // OR_Gate or_1, 32 bits wide
  assign and_2_out = or_1_out & 32'hfff;  // AND_Gate and_2, 32 bits wide
  Multiplexer #(.width(32), .enable("false")) multiplexer_12 (
    .in0(R1_t), .in1(PC_In_t), .out(multiplexer_12_out), .sel(JAL));
  Multiplexer #(.width(32), .enable("false")) multiplexer_13 (
    .in0(multiplexer_11_out), .in1(32'h4), .out(multiplexer_13_out), .sel(JAL));
  Register #(.width(32)) register_1 (.D(Instr_In_t), .Q(Instr_Out), .clk(in_1));  // open: en, clr
  Register #(.width(32)) register_2 (.D(PC_In_t), .Q(PC_Out), .clk(in_1));  // open: en, clr
  Register #(.width(32)) register_3 (.D(shifter_2_out), .Q(register_3_q), .clk(in_1));  // open: en, clr
  Register #(.width(32)) register_4 (.D(multiplexer_12_out), .Q(X), .clk(in_1));  // open: en, clr
  Register #(.width(32)) register_5 (.D(multiplexer_13_out), .Q(Y), .clk(in_1));  // open: en, clr
  Register #(.width(32)) register_6 (.D(R2_t), .Q(R2_Out), .clk(in_1));  // open: en, clr
  Register #(.width(32)) register_7 (.D(R1_t), .Q(register_7_q), .clk(in_1));  // open: en, clr
  Register #(.width(32)) register_8 (.D(and_2_out), .Q(register_8_q), .clk(in_1));  // open: en, clr
  Register #(.width(18)) register_9 (
    .D(multiplexer_9_out),
    .Q({SysCall_Out, register_9_q, RF_Din_Out, RegWB_2, RegW__Out, ALUop_Out, MemWeite_Out}), .clk(in_1));  // open: en, clr
  Register #(.width(1)) register_10 (.D(forecast_t), .Q(register_10_q), .clk(in_1));  // open: en, clr
  or or_2 (Jmp, register_9_q[14], or_4_out);
  not not_1 (not_1_out, Jmp);
  not not_2 (not_2_out, register_10_q);
  and and_3 (and_3_out, not_2_out, not_1_out);
  and and_4 (and_4_out, register_10_q, Jmp);
  or or_3 (or_3_out, and_4_out, and_3_out);
  Is_Branch is_branch_1 (.Instr(Instr_Out), .Is_Branch(Is_branch));
  not not_3 (not_3_out, or_3_out);
  Multiplexer #(.width(32), .enable("false")) multiplexer_14 (
    .in0({32{1'b0}}), .in1(Instr_Out), .out(Back_Instr), .sel(Is_branch));
  Multiplexer #(.width(32), .enable("false")) multiplexer_15 (
    .in0({32{1'b0}}), .in1(JMP_addr), .out(Branch_pc), .sel(Is_branch));
  Multiplexer #(.width(32), .enable("false")) multiplexer_16 (
    .in0({32{1'b0}}), .in1(PC_Out), .out(Back_pc), .sel(Is_branch));
  and and_5 (error, Is_branch, not_3_out);
  Adder #(.width(32)) adder_2 (.a(32'h4), .b(PC_Out), .out(adder_2_out));  // open: cin, cout
  not not_4 (not_4_out, EQUAL);
  and and_6 (and_6_out, not_4_out, register_9_q[15]);
  and and_7 (and_7_out, EQUAL, register_9_q[16]);
  Multiplexer #(.width(32), .enable("false")) multiplexer_17 (
    .in0({32{1'b0}}), .in1(register_3_q), .out(multiplexer_17_out), .sel(or_4_out));
  or or_4 (or_4_out, and_6_out, and_7_out);
  Adder #(.width(32)) adder_3 (.a(adder_2_out), .b(multiplexer_17_out), .out(adder_3_out));  // open: cin, cout
  Multiplexer #(.select(2), .width(32), .enable("false")) multiplexer_18 (
    .in0(adder_2_out), .in1(adder_3_out), .in2(register_8_q), .in3(register_7_q), .out(JMP_addr),
    .sel(register_9_q[14:13]));

  // Other names for the same wires on the sheet: Branch_pc_t[31:0] = JMP_addr; Clk = in_1
endmodule

module EX_MEM (
  input  in_1,
  input  [31:0] Instr_In,
  input  [31:0] PC_In,
  input  [31:0] Addr,
  input  [31:0] DM_Din,
  input  MemWrite,
  input  [31:0] LO_In,
  input  [1:0] RF_Din,
  input  [31:0] HI_In,
  input  RegWB,
  input  [4:0] RegW_num,
  input  SysCall,
  output [31:0] Instr_Out,
  output [31:0] PC_Out,
  output [31:0] Reg_Data,
  output [31:0] EX_Reg_Data,
  output [23:0] Addr_2,
  output [31:0] DM_Din_2,
  output [31:0] HI_Out,
  output [31:0] LO_Out,
  output MemWriteEn,
  output [1:0] RF_Din_2,
  output RegWB_2,
  output [4:0] RegW_num_2,
  output SysCall_Out
);

  Register #(.width(32)) register_1 (.D(Instr_In), .Q(Instr_Out), .clk(in_1));  // open: en, clr
  Register #(.width(32)) register_2 (.D(PC_In), .Q(PC_Out), .clk(in_1));  // open: en, clr
  Register #(.width(32)) register_3 (
    .D(Addr), .Q({Reg_Data[31:26], Addr_2, Reg_Data[1:0]}), .clk(in_1));  // open: en, clr
  Register #(.width(32)) register_4 (.D(DM_Din), .Q(DM_Din_2), .clk(in_1));  // open: en, clr
  Register #(.width(32)) register_5 (.D(HI_In), .Q(HI_Out), .clk(in_1));  // open: en, clr
  Register #(.width(32)) register_6 (.D(LO_In), .Q(LO_Out), .clk(in_1));  // open: en, clr
  Register #(.width(10)) register_7 (
    .D({SysCall, RegW_num, RegWB, RF_Din, MemWrite}),
    .Q({SysCall_Out, RegW_num_2, RegWB_2, RF_Din_2, MemWriteEn}), .clk(in_1));  // open: en, clr
  Multiplexer #(.select(2), .width(32), .enable("false")) multiplexer_1 (
    .in0(Addr), .in1({32{1'b0}}), .in2(HI_In), .in3(LO_In), .out(EX_Reg_Data), .sel(RF_Din));

  assign Reg_Data[25:2] = Addr_2;

  // Other names for the same wires on the sheet: Clk = in_1
endmodule

module MEM_WB (
  input  Clk,
  input  [31:0] LO_In,
  input  [31:0] Instr_In,
  input  [1:0] RF_Din,
  input  [31:0] HI_In,
  input  [31:0] PC_In,
  input  [31:0] Reg_Data,
  input  [31:0] DM_Out,
  input  SysCall,
  input  RegWB,
  input  [4:0] RegW_num,
  output [31:0] Instr_Out,
  output [31:0] PC_Out,
  output [31:0] WB_data,
  output RegWB_2,
  output [4:0] RegW_num_2,
  output SYSCALL_2,
  output [31:0] MEM_Reg_Data
);

  Register #(.width(32)) register_1 (.D(Instr_In), .Q(Instr_Out), .clk(Clk));  // open: en, clr
  Register #(.width(32)) register_2 (.D(PC_In), .Q(PC_Out), .clk(Clk));  // open: en, clr
  Multiplexer #(.select(2), .width(32), .enable("false")) multiplexer_1 (
    .in0(Reg_Data), .in1(DM_Out), .in2(HI_In), .in3(LO_In), .out(MEM_Reg_Data), .sel(RF_Din));
  Register #(.width(32)) register_3 (.D(MEM_Reg_Data), .Q(WB_data), .clk(Clk));  // open: en, clr
  Register #(.width(7)) register_4 (
    .D({SysCall, RegW_num, RegWB}), .Q({SYSCALL_2, RegW_num_2, RegWB_2}), .clk(Clk));  // open: en, clr
endmodule

module ConflictUnit (
  input  Branch,
  input  [31:0] EX_Instr,
  input  [31:0] MEM_Instr,
  input  [4:0] R1,
  input  [4:0] R2,
  input  EX_RWB,
  input  [4:0] EX_RW_num,
  input  [31:0] EX_Reg_Data,
  input  [31:0] MEM_Reg_Data,
  input  MEM_RWB,
  input  [4:0] MEM_RW_num,
  output IF_ID_Clr,
  output Jmp,
  output ID_EX_Clr,
  output Pc_ch,
  output Stop_Clk,
  output Conflict,
  output [31:0] R1_D_Out,
  output R1_Ch,
  output [31:0] R2_D_Out,
  output R2_Ch
);

  wire and_1_out, and_2_out, and_3_out, and_4_out, and_5_out, and_10_out, comparator_1_eq, comparator_2_eq,
       comparator_3_eq, comparator_4_eq, comparator_5_eq, comparator_6_eq, comparator_7_eq, comparator_8_eq,
       comparator_9_eq, comparator_10_eq, comparator_11_eq, comparator_12_eq, not_1_out, not_2_out,
       not_3_out, not_4_out, not_5_out, not_6_out, not_7_out, or_1_out;
  wire [1:0] and_6_out, and_8_out;

  Comparator #(.width(5)) comparator_1 (.a(EX_RW_num), .b(R1), .eq(comparator_1_eq));  // open: gt, lt
  Comparator #(.width(5)) comparator_2 (.a(R1), .b(MEM_RW_num), .eq(comparator_2_eq));  // open: gt, lt
  Comparator #(.width(5)) comparator_3 (.a(EX_RW_num), .b(R2), .eq(comparator_3_eq));  // open: gt, lt
  Comparator #(.width(5)) comparator_4 (.a(R2), .b(MEM_RW_num), .eq(comparator_4_eq));  // open: gt, lt
  and and_1 (and_1_out, EX_RWB, comparator_1_eq);
  and and_2 (and_2_out, comparator_2_eq, MEM_RWB);
  and and_3 (and_3_out, EX_RWB, comparator_3_eq);
  and and_4 (and_4_out, comparator_4_eq, MEM_RWB);
  Comparator #(.width(5)) comparator_5 (.a(R1), .b(EX_RW_num), .eq(comparator_5_eq));  // open: gt, lt
  Comparator #(.width(5)) comparator_6 (.a(R2), .b(EX_RW_num), .eq(comparator_6_eq));  // open: gt, lt
  // Probe on EX_Instr[31:26]
  Comparator #(.width(32)) comparator_7 (.a(EX_Instr), .b({32{1'b0}}), .eq(comparator_7_eq));  // open: gt, lt
  Comparator #(.width(32)) comparator_8 (.a(MEM_Instr), .b({32{1'b0}}), .eq(comparator_8_eq));  // open: gt, lt
  Comparator #(.width(32)) comparator_9 (.a(EX_Instr), .b({32{1'b0}}), .eq(comparator_9_eq));  // open: gt, lt
  Comparator #(.width(32)) comparator_10 (.a(MEM_Instr), .b({32{1'b0}}), .eq(comparator_10_eq));  // open: gt, lt
  or or_1 (or_1_out, comparator_5_eq, comparator_6_eq);
  not not_1 (not_1_out, Branch);
  not not_2 (not_2_out, comparator_7_eq);
  not not_3 (not_3_out, comparator_8_eq);
  not not_4 (not_4_out, comparator_9_eq);
  not not_5 (not_5_out, comparator_10_eq);
  and and_5 (and_5_out, EX_RWB, or_1_out);
  Comparator #(.width(32)) comparator_11 (.a(EX_Instr), .b({32{1'b0}}), .eq(comparator_11_eq));  // open: gt, lt
  Comparator #(.width(6)) comparator_12 (.a(6'b100011), .b(EX_Instr[31:26]), .eq(comparator_12_eq));  // open: gt, lt
  and and_6 (and_6_out[0], and_1_out, not_1_out, not_2_out);
  and and_7 (and_6_out[1], and_2_out, not_1_out, not_3_out);
  and and_8 (and_8_out[0], and_3_out, not_1_out, not_4_out);
  and and_9 (and_8_out[1], and_4_out, not_1_out, not_5_out);
  not not_6 (not_6_out, comparator_11_eq);
  Multiplexer #(.select(2), .width(32), .disabled(0), .enable("false")) multiplexer_1 (
    .in0({32{1'b0}}), .in1(EX_Reg_Data), .in2(MEM_Reg_Data), .in3(EX_Reg_Data), .out(R1_D_Out),
    .sel(and_6_out));
  or or_2 (R1_Ch, and_6_out[1], and_6_out[0]);
  Multiplexer #(.select(2), .width(32), .disabled(0), .enable("false")) multiplexer_2 (
    .in0({32{1'b0}}), .in1(EX_Reg_Data), .in2(MEM_Reg_Data), .in3(EX_Reg_Data), .out(R2_D_Out),
    .sel(and_8_out));
  or or_3 (R2_Ch, and_8_out[1], and_8_out[0]);
  and and_10 (and_10_out, and_5_out, comparator_12_eq, not_6_out);
  not not_7 (not_7_out, Branch);
  and and_11 (Conflict, and_10_out, not_7_out);
  or or_4 (ID_EX_Clr, Branch, Conflict);
  not not_8 (Stop_Clk, Conflict);

  assign IF_ID_Clr = Branch;
  assign Jmp = Branch;
  assign Pc_ch = Branch;
endmodule

// State
module _2bit_state (
  input  success,
  input  clk,
  input  enable,
  output [1:0] state_out
);

  wire and_1_out, and_2_out, and_3_out, or_1_out;

  D_Flip_Flop y2 (.clk(clk), .D(or_1_out), .Q(state_out[1]), .en(enable));  // open: Qn, preset, reset
  D_Flip_Flop y1 (.clk(clk), .D(success), .Q(state_out[0]), .en(enable));  // open: Qn, preset, reset
  and and_1 (and_1_out, success, state_out[0]);
  and and_2 (and_2_out, state_out[1], success);
  and and_3 (and_3_out, state_out[1], state_out[0]);
  or or_1 (or_1_out, and_1_out, and_2_out, and_3_out);
endmodule

module BTB (
  input  Clk,
  input  Success,
  input  [31:0] Back_pc,
  input  [31:0] Branch_pc,
  input  [31:0] Pc_In,
  input  [31:0] Current_Instr,
  input  [31:0] Back_Instr,
  output [31:0] Pc_Out,
  output Forecast_Jmp
);

  wire and_1_out, and_2_out, and_3_out, and_4_out, and_5_out, and_6_out, and_7_out, and_8_out, and_9_out,
       and_10_out, and_11_out, and_12_out, and_13_out, and_14_out, and_15_out, and_16_out, Back_match,
       comparator_1_eq, comparator_2_eq, comparator_3_eq, comparator_4_eq, comparator_5_eq, comparator_6_eq,
       comparator_7_eq, comparator_8_eq, comparator_9_eq, demultiplexer_1_out0, demultiplexer_1_out1,
       demultiplexer_1_out2, demultiplexer_1_out3, demultiplexer_2_out0, demultiplexer_2_out1,
       demultiplexer_2_out2, demultiplexer_2_out3, En0, En1, En2, En3, is_branch_1_is_branch, match,
       not_1_out, not_2_out, not_3_out, not_4_out, not_5_out, not_6_out, valid0, valid1, valid2, valid3;
  wire [1:0] max_1_out, n2bit_state_1_state_out, n2bit_state_2_state_out, n2bit_state_3_state_out,
       n2bit_state_4_state_out, priority_encoder_1_out, priority_encoder_2_out;
  wire [7:0] Count0_q, Count1_q, Count2_q, Count3_q;
  wire [31:0] adder_1_out, multiplexer_1_out, Next_Addr0_q, Next_Addr1_q, Next_Addr2_q, Next_Addr3_q, PC0,
       PC1, PC2, PC3;

  Comparator #(.width(32)) comparator_1 (.a(Back_Instr), .b({32{1'b0}}), .eq(comparator_1_eq));  // open: gt, lt
  // Probe on Count0_q
  not not_1 (not_1_out, Back_match);
  Demultiplexer #(.select(2), .disabled(0)) demultiplexer_1 (
    .out0(demultiplexer_1_out0), .out1(demultiplexer_1_out1), .out2(demultiplexer_1_out2),
    .out3(demultiplexer_1_out3), .in(1'b1), .sel(max_1_out), .en(not_1_out));
  Demultiplexer #(.select(2), .disabled(0)) demultiplexer_2 (
    .out0(demultiplexer_2_out0), .out1(demultiplexer_2_out1), .out2(demultiplexer_2_out2),
    .out3(demultiplexer_2_out3), .in(1'b1), .sel(priority_encoder_1_out), .en(Back_match));
  not not_2 (not_2_out, comparator_1_eq);
  and and_1 (and_1_out, not_2_out, En0);
  Register #(.width(32)) u_Pc0 (.D(Back_pc), .en(and_1_out), .Q(PC0), .clk(Clk));  // open: clr
  Register #(.width(1)) u_Valid0 (.D(1'b1), .en(and_1_out), .Q(valid0), .clk(Clk));  // open: clr
  _2bit_state u_2bit_state_1 (.success(Success), .clk(Clk), .state_out(n2bit_state_1_state_out), .enable(and_1_out));
  Register #(.width(32)) Next_Addr0 (.D(Branch_pc), .en(and_1_out), .Q(Next_Addr0_q), .clk(Clk));  // open: clr
  Counter Count0 (.load(and_1_out), .D({8{1'b0}}), .count(not_3_out), .Q(Count0_q), .clk(Clk));  // open: carry, clr
  not not_3 (not_3_out, and_1_out);
  // Probe on Count1_q
  Comparator #(.width(32)) comparator_2 (.a(Back_pc), .b(PC0), .eq(comparator_2_eq));  // open: gt, lt
  Comparator #(.width(32)) comparator_3 (.a(Pc_In), .b(PC0), .eq(comparator_3_eq));  // open: gt, lt
  and and_2 (and_2_out, n2bit_state_1_state_out[0], n2bit_state_1_state_out[1]);
  or or_1 (En0, demultiplexer_1_out0, demultiplexer_2_out0);
  and and_3 (and_3_out, comparator_2_eq, valid0);
  and and_4 (and_4_out, not_2_out, En1);
  and and_5 (and_5_out, comparator_3_eq, valid0, and_2_out);
  Register #(.width(32)) u_Pc1 (.D(Back_pc), .en(and_4_out), .Q(PC1), .clk(Clk));  // open: clr
  Register #(.width(1)) u_Valid1 (.D(1'b1), .en(and_4_out), .Q(valid1), .clk(Clk));  // open: clr
  _2bit_state u_2bit_state_2 (.success(Success), .clk(Clk), .state_out(n2bit_state_2_state_out), .enable(and_4_out));
  Register #(.width(32)) Next_Addr1 (.D(Branch_pc), .en(and_4_out), .Q(Next_Addr1_q), .clk(Clk));  // open: clr
  not not_4 (not_4_out, and_4_out);
  or or_2 (En1, demultiplexer_1_out1, demultiplexer_2_out1);
  Comparator #(.width(32)) comparator_4 (.a(Back_pc), .b(PC1), .eq(comparator_4_eq));  // open: gt, lt
  Comparator #(.width(32)) comparator_5 (.a(Pc_In), .b(PC1), .eq(comparator_5_eq));  // open: gt, lt
  and and_6 (and_6_out, n2bit_state_2_state_out[0], n2bit_state_2_state_out[1]);
  Counter Count1 (.load(and_4_out), .D({8{1'b0}}), .count(not_4_out), .Q(Count1_q), .clk(Clk));  // open: carry, clr
  or or_3 (En2, demultiplexer_1_out2, demultiplexer_2_out2);
  and and_7 (and_7_out, comparator_4_eq, valid1);
  and and_8 (and_8_out, not_2_out, En2);
  and and_9 (and_9_out, comparator_5_eq, valid1, and_6_out);
  not not_5 (not_5_out, and_8_out);
  or or_4 (En3, demultiplexer_1_out3, demultiplexer_2_out3);
  Comparator #(.width(32)) comparator_6 (.a(Back_pc), .b(PC2), .eq(comparator_6_eq));  // open: gt, lt
  Comparator #(.width(32)) comparator_7 (.a(Pc_In), .b(PC2), .eq(comparator_7_eq));  // open: gt, lt
  Register #(.width(32)) u_Pc2 (.D(Back_pc), .en(and_8_out), .Q(PC2), .clk(Clk));  // open: clr
  Register #(.width(1)) u_Valid2 (.D(1'b1), .en(and_8_out), .Q(valid2), .clk(Clk));  // open: clr
  and and_10 (and_10_out, n2bit_state_3_state_out[0], n2bit_state_3_state_out[1]);
  _2bit_state u_2bit_state_3 (.success(Success), .clk(Clk), .state_out(n2bit_state_3_state_out), .enable(and_8_out));
  Register #(.width(32)) Next_Addr2 (.D(Branch_pc), .en(and_8_out), .Q(Next_Addr2_q), .clk(Clk));  // open: clr
  Counter Count2 (.load(and_8_out), .D({8{1'b0}}), .count(not_5_out), .Q(Count2_q), .clk(Clk));  // open: carry, clr
  and and_11 (and_11_out, comparator_6_eq, valid2);
  and and_12 (and_12_out, not_2_out, En3);
  and and_13 (and_13_out, comparator_7_eq, valid2, and_10_out);
  not not_6 (not_6_out, and_12_out);
  Comparator #(.width(32)) comparator_8 (.a(Back_pc), .b(PC3), .eq(comparator_8_eq));  // open: gt, lt
  Register #(.width(32)) u_Pc3 (.D(Back_pc), .en(and_12_out), .Q(PC3), .clk(Clk));  // open: clr
  Register #(.width(1)) u_Valid3 (.D(1'b1), .en(and_12_out), .Q(valid3), .clk(Clk));  // open: clr
  _2bit_state u_2bit_state_4 (.success(Success), .clk(Clk), .state_out(n2bit_state_4_state_out), .enable(and_12_out));
  Register #(.width(32)) Next_Addr3 (.D(Branch_pc), .en(and_12_out), .Q(Next_Addr3_q), .clk(Clk));  // open: clr
  Counter Count3 (.load(and_12_out), .D({8{1'b0}}), .count(not_6_out), .Q(Count3_q), .clk(Clk));  // open: carry, clr
  Max max_1 (.In0(Count0_q), .In1(Count1_q), .In2(Count2_q), .In3(Count3_q), .Out(max_1_out));
  and and_14 (and_14_out, comparator_8_eq, valid3);
  Comparator #(.width(32)) comparator_9 (.a(Pc_In), .b(PC3), .eq(comparator_9_eq));  // open: gt, lt
  and and_15 (and_15_out, comparator_9_eq, valid3, and_16_out);
  and and_16 (and_16_out, n2bit_state_4_state_out[0], n2bit_state_4_state_out[1]);
  Priority_Encoder #(.select(2)) priority_encoder_1 (
    .in0(and_3_out), .in1(and_7_out), .in2(and_11_out), .in3(and_14_out), .out(priority_encoder_1_out),
    .gs(Back_match));  // open: en_out, en_in
  Is_Branch is_branch_1 (.Instr(Current_Instr), .Is_Branch(is_branch_1_is_branch));
  // Probe on Count2_q
  // Probe on Count3_q
  Adder #(.width(32)) adder_1 (.a(Pc_In), .b(32'h4), .out(adder_1_out));  // open: cin, cout
  Multiplexer #(.select(2), .width(32), .enable("false")) multiplexer_1 (
    .in0(Next_Addr0_q), .in1(Next_Addr1_q), .in2(Next_Addr2_q), .in3(Next_Addr3_q), .out(multiplexer_1_out),
    .sel(priority_encoder_2_out));
  Priority_Encoder #(.select(2)) priority_encoder_2 (
    .in0(and_5_out), .in1(and_9_out), .in2(and_13_out), .in3(and_15_out), .out(priority_encoder_2_out),
    .gs(match));  // open: en_out, en_in
  and and_17 (Forecast_Jmp, is_branch_1_is_branch, match);
  Multiplexer #(.width(32), .enable("false")) multiplexer_2 (
    .in0(adder_1_out), .in1(multiplexer_1_out), .out(Pc_Out), .sel(Forecast_Jmp));
endmodule

module Is_Branch (
  input  [31:0] Instr,
  output Is_Branch
);

  wire and_1_out, comparator_1_eq, comparator_2_eq, comparator_3_eq, comparator_4_eq, comparator_5_eq,
       comparator_6_eq;

  Comparator #(.width(6), .mode("unsigned")) comparator_1 (
    .a(Instr[31:26]), .b(6'b000010), .eq(comparator_1_eq));  // open: gt, lt
  Comparator #(.width(6), .mode("unsigned")) comparator_2 (
    .a(Instr[31:26]), .b(6'b000011), .eq(comparator_2_eq));  // open: gt, lt
  Comparator #(.width(6)) comparator_3 (.a(Instr[31:26]), .b({6{1'b0}}), .eq(comparator_3_eq));  // open: gt, lt
  Comparator #(.width(6)) comparator_4 (.a(Instr[5:0]), .b(6'b001000), .eq(comparator_4_eq));  // open: gt, lt
  Comparator #(.width(6), .mode("unsigned")) comparator_5 (
    .a(Instr[31:26]), .b(6'b000100), .eq(comparator_5_eq));  // open: gt, lt
  Comparator #(.width(6), .mode("unsigned")) comparator_6 (
    .a(Instr[31:26]), .b(6'b000101), .eq(comparator_6_eq));  // open: gt, lt
  and and_1 (and_1_out, comparator_3_eq, comparator_4_eq);
  or or_1 (Is_Branch, comparator_1_eq, comparator_2_eq, and_1_out, comparator_5_eq, comparator_6_eq);

  // Notes on the sheet:
  //   j
  //   jal
  //   jr
  //   beq
  //   bne
endmodule

module Max (
  input  [7:0] In0,
  input  [7:0] In1,
  input  [7:0] In2,
  input  [7:0] In3,
  output [1:0] Out
);

  wire and_1_out, and_2_out, and_3_out, and_4_out, comparator_1_eq, comparator_1_gt, comparator_2_eq,
       comparator_2_gt, comparator_3_eq, comparator_3_gt, comparator_4_eq, comparator_4_gt, comparator_5_eq,
       comparator_5_gt, comparator_6_eq, comparator_6_gt, comparator_7_eq, comparator_7_gt, comparator_8_eq,
       comparator_8_gt, comparator_9_eq, comparator_9_gt, comparator_10_eq, comparator_10_gt,
       comparator_11_eq, comparator_11_gt, comparator_12_eq, comparator_12_gt, or_1_out, or_2_out, or_3_out,
       or_4_out, or_5_out, or_6_out, or_7_out, or_8_out, or_9_out, or_10_out, or_11_out, or_12_out;

  Comparator #(.mode("unsigned")) comparator_1 (
    .a(In0), .b(In1), .gt(comparator_1_gt), .eq(comparator_1_eq));  // open: lt
  Comparator #(.mode("unsigned")) comparator_2 (
    .a(In0), .b(In2), .gt(comparator_2_gt), .eq(comparator_2_eq));  // open: lt
  Comparator #(.mode("unsigned")) comparator_3 (
    .a(In0), .b(In3), .gt(comparator_3_gt), .eq(comparator_3_eq));  // open: lt
  Comparator #(.mode("unsigned")) comparator_4 (
    .a(In1), .b(In0), .gt(comparator_4_gt), .eq(comparator_4_eq));  // open: lt
  Comparator #(.mode("unsigned")) comparator_5 (
    .a(In1), .b(In2), .gt(comparator_5_gt), .eq(comparator_5_eq));  // open: lt
  Comparator #(.mode("unsigned")) comparator_6 (
    .a(In1), .b(In3), .gt(comparator_6_gt), .eq(comparator_6_eq));  // open: lt
  Comparator #(.mode("unsigned")) comparator_7 (
    .a(In2), .b(In0), .gt(comparator_7_gt), .eq(comparator_7_eq));  // open: lt
  Comparator #(.mode("unsigned")) comparator_8 (
    .a(In2), .b(In1), .gt(comparator_8_gt), .eq(comparator_8_eq));  // open: lt
  Comparator #(.mode("unsigned")) comparator_9 (
    .a(In2), .b(In3), .gt(comparator_9_gt), .eq(comparator_9_eq));  // open: lt
  Comparator #(.mode("unsigned")) comparator_10 (
    .a(In3), .b(In0), .gt(comparator_10_gt), .eq(comparator_10_eq));  // open: lt
  Comparator #(.mode("unsigned")) comparator_11 (
    .a(In3), .b(In1), .gt(comparator_11_gt), .eq(comparator_11_eq));  // open: lt
  Comparator #(.mode("unsigned")) comparator_12 (
    .a(In3), .b(In2), .gt(comparator_12_gt), .eq(comparator_12_eq));  // open: lt
  or or_1 (or_1_out, comparator_1_gt, comparator_1_eq);
  or or_2 (or_2_out, comparator_2_gt, comparator_2_eq);
  or or_3 (or_3_out, comparator_3_gt, comparator_3_eq);
  or or_4 (or_4_out, comparator_4_gt, comparator_4_eq);
  or or_5 (or_5_out, comparator_5_gt, comparator_5_eq);
  or or_6 (or_6_out, comparator_6_gt, comparator_6_eq);
  or or_7 (or_7_out, comparator_7_gt, comparator_7_eq);
  or or_8 (or_8_out, comparator_8_gt, comparator_8_eq);
  or or_9 (or_9_out, comparator_9_gt, comparator_9_eq);
  or or_10 (or_10_out, comparator_10_gt, comparator_10_eq);
  or or_11 (or_11_out, comparator_11_gt, comparator_11_eq);
  or or_12 (or_12_out, comparator_12_gt, comparator_12_eq);
  and and_1 (and_1_out, or_1_out, or_2_out, or_3_out);
  and and_2 (and_2_out, or_4_out, or_5_out, or_6_out);
  and and_3 (and_3_out, or_7_out, or_8_out, or_9_out);
  and and_4 (and_4_out, or_10_out, or_11_out, or_12_out);
  Priority_Encoder #(.select(2)) priority_encoder_1 (
    .in0(and_1_out), .in1(and_2_out), .in2(and_3_out), .in3(and_4_out), .out(Out));  // open: gs, en_out, en_in
endmodule
