// Logisim project Main.circ as structural Verilog
module Single (
  input  [4:0] in_1
);

  wire alu_1_equal, and_2_out, and_3_out, and_4_out, Clk, clock_1_out, comparator_1_eq, controlunit_1_beq,
       controlunit_1_bne, controlunit_1_jal, controlunit_1_memwrite, controlunit_1_r1_num,
       controlunit_1_regwirteback, hilocontrol_1_hilocontrol, not_1_out, not_2_out, or_2_out, SysCall;
  wire [1:0] ALUSrc, controlunit_1_pccontrol, controlunit_1_rf_din, controlunit_1_w_num;
  wire [3:0] ALUop, multiplexer_2_out, multiplexer_2_out_3, multiplexer_2_out_4, multiplexer_2_out_5;
  wire [4:0] instrdecode_1_shamt, multiplexer_4_out, R1, R2, rd, rs;
  wire [5:0] instrdecode_1_funct, instrdecode_1_opcode;
  wire [15:0] instrdecode_1_imm;
  wire [23:4] multiplexer_2_out_2;
  wire [25:0] instrdecode_1_addr;
  wire [31:0] a0, adder_1_out, adder_2_out, adder_3_out, alu_1_result_2, and_1_out, bit_extender_1_out,
       bit_extender_2_out, bit_extender_3_out, bit_extender_4_out, counter_1_q, Dnug_value, hilo_1_hi_out,
       hilo_1_lo_out, multiplexer_1_out, multiplexer_6_out, multiplexer_9_out, multiplexer_10_out, or_1_out,
       ram_1_data, Reg_q, regfile_1_reg1, regfile_1_reg2_2, Result, rom_1_data, shifter_1_out, shifter_2_out,
       subtractor_1_out, v0, X, Y;

  Multiplexer #(.select(2), .width(32), .enable("false")) multiplexer_1 (
    .in0(adder_1_out), .in1(adder_3_out), .in2(subtractor_1_out), .in3(regfile_1_reg1),
    .out(multiplexer_1_out), .sel(controlunit_1_pccontrol));
  // Probe on Result
  Register #(.width(32)) Reg (.D(multiplexer_1_out), .Q(Reg_q), .clk(Clk));  // open: en, clr
  Subtractor #(.width(32)) subtractor_1 (.a(or_1_out), .b(32'h3000), .out(subtractor_1_out));  // open: bin, bout
  assign or_1_out = shifter_1_out | and_1_out;  // OR_Gate or_1, 32 bits wide
  assign and_1_out = adder_1_out & 32'hf0000000;  // AND_Gate and_1, 32 bits wide
  Comparator #(.width(32)) comparator_1 (.a(v0), .b(32'ha), .eq(comparator_1_eq));  // open: gt, lt
  // Probe on rs
  // Probe on rs
  // Probe on R2
  // Probe on R2
  // Probe on rd
  // Probe on rd
  Adder #(.width(32)) adder_1 (.a(Reg_q), .b(32'h4), .out(adder_1_out));  // open: cin, cout
  and and_2 (and_2_out, comparator_1_eq, SysCall);
  ROM #(.addrWidth(24), .dataWidth(32)) rom_1 (.addr(Reg_q[25:2]), .data(rom_1_data));  // open: sel
  Hex_Digit_Display hex_digit_display_1 (.value(multiplexer_2_out_5));  // open: dp
  not not_1 (not_1_out, and_2_out);
  InstrDecode instrdecode_1 (
    .rd(rd), .rt(R2), .Addr(instrdecode_1_addr), .IMM(instrdecode_1_imm), .IND(rom_1_data), .rs(rs),
    .Funct(instrdecode_1_funct), .OpCode(instrdecode_1_opcode), .shamt(instrdecode_1_shamt));
  Hex_Digit_Display hex_digit_display_2 (.value(multiplexer_2_out_2[23:20]));  // open: dp
  Hex_Digit_Display hex_digit_display_3 (.value(multiplexer_2_out_4));  // open: dp
  // Probe on X
  // Probe on Y
  assign bit_extender_1_out = {{6{instrdecode_1_addr[25]}}, instrdecode_1_addr};  // Bit_Extender bit_extender_1
  Shifter #(.width(32)) shifter_1 (.in(bit_extender_1_out), .\dist (5'b00010), .out(shifter_1_out));
  Hex_Digit_Display hex_digit_display_4 (.value(multiplexer_2_out_2[19:16]));  // open: dp
  Hex_Digit_Display hex_digit_display_5 (.value(multiplexer_2_out_3));  // open: dp
  Multiplexer #(.width(32), .enable("false")) multiplexer_2 (
    .in1(a0),
    .out({multiplexer_2_out_5, multiplexer_2_out_4, multiplexer_2_out_2[23:16], multiplexer_2_out_3, multiplexer_2_out_2[11:4], multiplexer_2_out}),
    .sel(not_1_out));  // open: in0
  assign bit_extender_2_out = {{27{1'b0}}, instrdecode_1_shamt};  // Bit_Extender bit_extender_2
  Hex_Digit_Display hex_digit_display_6 (.value(multiplexer_2_out_2[7:4]));  // open: dp
  Hex_Digit_Display hex_digit_display_7 (.value(multiplexer_2_out_2[11:8]));  // open: dp
  Multiplexer #(.width(5), .disabled(0), .enable("false")) multiplexer_3 (
    .in0(rs), .in1(R2), .out(R1), .sel(controlunit_1_r1_num));
  ControlUnit controlunit_1 (
    .RegWirteBack(controlunit_1_regwirteback), .ALUop(ALUop), .PcControl(controlunit_1_pccontrol),
    .W_num(controlunit_1_w_num), .R1_num(controlunit_1_r1_num), .RF_Din(controlunit_1_rf_din),
    .MemWrite(controlunit_1_memwrite), .ALUsrc(ALUSrc), .SysCall(SysCall), .BNE(controlunit_1_bne),
    .BEQ(controlunit_1_beq), .JAl(controlunit_1_jal), .OpCode(instrdecode_1_opcode),
    .Funct(instrdecode_1_funct));
  Hex_Digit_Display hex_digit_display_8 (.value(multiplexer_2_out));  // open: dp
  // Probe on R1
  // Probe on R2
  // Probe on ALUop
  // Probe on ALUSrc
  // Probe on Dnug_value
  Multiplexer #(.select(2), .width(5), .enable("false")) multiplexer_4 (
    .in0(R2), .in1({5{1'b1}}), .in2(rd), .out(multiplexer_4_out), .sel(controlunit_1_w_num));  // open: in3
  Multiplexer #(.enable("false")) multiplexer_5 (.in0(clock_1_out), .in1(1'b0), .out(Clk), .sel(and_2_out));
  // Probe on in_1
  Clock clock_1 (.out(clock_1_out));
  RegFile regfile_1 (
    .Reg1_num(R1), .Reg2(R2), .Write_Reg_num(multiplexer_4_out), .Din(multiplexer_9_out),
    .Write_Enable(controlunit_1_regwirteback), .Clock(Clk), .Reg1(regfile_1_reg1), .Reg2_2(regfile_1_reg2_2),
    .v0(v0), .a0(a0), .in_3(in_1), .DebugValue(Dnug_value));
  assign bit_extender_3_out = {{16{instrdecode_1_imm[15]}}, instrdecode_1_imm};  // Bit_Extender bit_extender_3
  assign bit_extender_4_out = {{16{1'b0}}, instrdecode_1_imm};  // Bit_Extender bit_extender_4
  Multiplexer #(.select(2), .width(32), .enable("false")) multiplexer_6 (
    .in0(regfile_1_reg2_2), .in1(bit_extender_3_out), .in2(bit_extender_4_out), .in3(bit_extender_2_out),
    .out(multiplexer_6_out), .sel(ALUSrc));
  Shifter #(.width(32)) shifter_2 (.in(bit_extender_3_out), .\dist (5'b00010), .out(shifter_2_out));
  HILOControl hilocontrol_1 (.ALUop(ALUop), .HILOControl(hilocontrol_1_hilocontrol));
  Multiplexer #(.width(32), .enable("false")) multiplexer_7 (
    .in0(regfile_1_reg1), .in1(Reg_q), .out(X), .sel(controlunit_1_jal));
  Multiplexer #(.width(32), .enable("false")) multiplexer_8 (
    .in0(multiplexer_6_out), .in1(32'h4), .out(Y), .sel(controlunit_1_jal));
  HILO hilo_1 (
    .HI_In(alu_1_result_2), .LO_In(Result), .Clk(Clk), .Control(hilocontrol_1_hilocontrol),
    .HI_Out(hilo_1_hi_out), .LO_Out(hilo_1_lo_out));
  ALU alu_1 (
    .AluOP(ALUop), .X(X), .Equal(alu_1_equal), .Result(Result), .Y(Y), .Result_2(alu_1_result_2));  // open: Signed_Overflow, UnSigned_Overflow
  Multiplexer #(.select(2), .width(32), .enable("false")) multiplexer_9 (
    .in0(Result), .in1(ram_1_data), .in2(hilo_1_hi_out), .in3(hilo_1_lo_out), .out(multiplexer_9_out),
    .sel(controlunit_1_rf_din));
  not not_2 (not_2_out, alu_1_equal);
  Counter #(.width(32), .max('hffffffff), .trigger("falling")) counter_1 (
    .load(1'b0), .D(32'h1), .count(1'b1), .Q(counter_1_q), .clk(Clk));  // open: carry, clr
  and and_3 (and_3_out, not_2_out, controlunit_1_bne);
  or or_2 (or_2_out, and_3_out, and_4_out);
  and and_4 (and_4_out, controlunit_1_beq, alu_1_equal);
  Adder #(.width(32)) adder_2 (.a(counter_1_q), .b(32'h1), .out(adder_2_out));  // open: cin, cout
  Multiplexer #(.width(32), .enable("false")) multiplexer_10 (
    .in0({32{1'b0}}), .in1(shifter_2_out), .out(multiplexer_10_out), .sel(or_2_out));
  // Probe on adder_2_out
  RAM #(.addrWidth(24), .dataWidth(32), .bus("separate")) ram_1 (
    .addr(Result[25:2]), .din(regfile_1_reg2_2), .data(ram_1_data), .str(controlunit_1_memwrite), .clk(Clk),
    .ld(controlunit_1_rf_din[0]));  // open: sel, clr
  Adder #(.width(32)) adder_3 (.a(multiplexer_10_out), .b(adder_1_out), .out(adder_3_out));  // open: cin, cout

  // Other names for the same wires on the sheet: Denug[4:0] = in_1; rt[4:0] = R2

  // Notes on the sheet:
  //   contents of rom_1 (hex, n*v repeats v):
  //   2010ffff 20110000 ae300000 22100001 22310004 ae300000 22100001 22310004 ae300000 22100001 22310004
  //   ae300000 22100001 22310004 ae300000 22100001 22310004 ae300000 22100001 22310004 ae300000 22100001
  //   22310004 ae300000 22100001 22310004 ae300000 22100001 22310004 ae300000 22100001 22310004 ae300000
  //   22100001 22310004 ae300000 22100001 22310004 ae300000 22100001 22310004 ae300000 22100001 22310004
  //   ae300000 22100001 22310004 ae300000 22100001 22310004 22100001 8020 2011003c 8e130000 8e340000
  //   274402a 11000002 ae330000 ae140000 2231fffc 1611fff8 102020 20020022 c 22100004 2011003c 1611fff2
  //   2002000a c
endmodule
