// Logisim project alu.circ as structural Verilog: 9 circuits, main circuit ALU
module ALU (
  input  [31:0] X,
  input  [31:0] Y,
  input  [3:0] AluOP,
  output Signed_Overflow,
  output UnSigned_Overflow,
  output Equal,
  output [31:0] Result,
  output [31:0] Result_2
);

  wire add_1_cf, add_1_of, comparator_1_lt, comparator_2_lt, sub_1_cf, sub_1_of;
  wire [31:0] add_1_out, and_out, bit_extender_1_out, bit_extender_2_out, bit_extender_3_out, div_1_out1,
       div_1_out2, mul_1_out1, mul_1_out2, not_1_out, or_out, sal_1_out_3, shl_1_out_3, shr_1_out_3,
       sub_1_out, xor_out;

  // Probe on X
  // Probe on X
  // Probe on Y
  // Probe on Y
  MUL mul_1 (.X(X), .Y(Y), .Out2(mul_1_out2), .Out1(mul_1_out1));
  SHL shl_1 (.X(X), .Y(Y), .out_3(shl_1_out_3));
  SAL sal_1 (.X(X), .Y(Y), .out_3(sal_1_out_3));
  SHR shr_1 (.X(X), .Y(Y), .out_3(shr_1_out_3));
  DIV div_1 (.X(X), .Y(Y), .Out1(div_1_out1), .Out2(div_1_out2));
  assign and_out = X & Y;  // AND_Gate and, 32 bits wide
  assign or_out = X | Y;  // OR_Gate or, 32 bits wide
  assign xor_out = X ^ Y;  // XOR_Gate xor, 32 bits wide
  Comparator #(.width(32)) comparator_1 (.a(X), .b(Y), .eq(Equal), .lt(comparator_1_lt));  // open: gt
  Comparator #(.width(32), .mode("unsigned")) comparator_2 (.a(X), .b(Y), .lt(comparator_2_lt));  // open: gt, eq
  Multiplexer #(.select(4)) multiplexer_1 (
    .in0(1'b0), .in1(1'b0), .in2(1'b0), .in3(1'b0), .in4(1'b0), .in5(add_1_cf), .in6(sub_1_cf), .in7(1'b0),
    .in8(1'b0), .in9(1'b0), .in10(1'b0), .in11(1'b0), .in12(1'b0), .in13(1'b0), .in14(1'b0), .in15(1'b0),
    .out(UnSigned_Overflow), .sel(AluOP), .en(1'b1));
  // Probe on AluOP
  ADD add_1 (.X(X), .out(add_1_out), .OF(add_1_of), .in_2(Y), .CF(add_1_cf));
  SUB sub_1 (.out(sub_1_out), .X(X), .in_2(Y), .CF(sub_1_cf), .OF(sub_1_of));
  // Probe on Result
  // Probe on Result
  assign not_1_out = ~or_out;  // NOT_Gate not_1, 32 bits wide
  assign bit_extender_1_out = {{31{1'b0}}, comparator_1_lt};  // Bit_Extender bit_extender_1
  assign bit_extender_2_out = {{31{1'b0}}, comparator_2_lt};  // Bit_Extender bit_extender_2
  Multiplexer #(.select(4)) multiplexer_2 (
    .in0(1'b0), .in1(1'b0), .in2(1'b0), .in3(1'b0), .in4(1'b0), .in5(add_1_of), .in6(sub_1_of), .in7(1'b0),
    .in8(1'b0), .in9(1'b0), .in10(1'b0), .in11(1'b0), .in12(1'b0), .in13(1'b0), .in14(1'b0), .in15(1'b0),
    .out(Signed_Overflow), .sel(AluOP), .en(1'b1));
  // Probe on Result_2
  assign bit_extender_3_out = {{31{1'b0}}, 1'b0};  // Bit_Extender bit_extender_3
  Multiplexer #(.select(4), .width(32)) multiplexer_3 (
    .in0(shl_1_out_3), .in1(sal_1_out_3), .in2(shr_1_out_3), .in3(mul_1_out1), .in4(div_1_out1),
    .in5(add_1_out), .in6(sub_1_out), .in7(and_out), .in8(or_out), .in9(xor_out), .in10(not_1_out),
    .in11(bit_extender_1_out), .in12(bit_extender_2_out), .in13(bit_extender_3_out),
    .in14(bit_extender_3_out), .in15(bit_extender_3_out), .out(Result), .sel(AluOP), .en(1'b1));
  Multiplexer #(.select(4), .width(32)) multiplexer_4 (
    .in0(bit_extender_3_out), .in1(bit_extender_3_out), .in2(bit_extender_3_out), .in3(mul_1_out2),
    .in4(div_1_out2), .in5(bit_extender_3_out), .in6(bit_extender_3_out), .in7(bit_extender_3_out),
    .in8(bit_extender_3_out), .in9(bit_extender_3_out), .in10(bit_extender_3_out), .in11(bit_extender_3_out),
    .in12(bit_extender_3_out), .in13(bit_extender_3_out), .in14(bit_extender_3_out),
    .in15(bit_extender_3_out), .out(Result_2), .sel(AluOP), .en(1'b1));

  // Other names for the same wires on the sheet: CF = UnSigned_Overflow; OF = Signed_Overflow;
  //   Result2[31:0] = Result_2; S[3:0] = AluOP

  // Notes on the sheet:
  //   不要改变此引脚区域内容，也不要改变ALU封装形式
  //   输入引脚
  //   请在下方利用上方输入输出引脚的隧道信号构建ALU电路，ctrl+d复制选择部件
  //   华中科技大学计算机学院 计算机组成原理，鸣谢加州大学伯克利CS61C课程
  //   输出引脚
  //   探测区域
endmodule

module \演示电路  (
  input  [31:0] X,
  input  [31:0] Y,
  input  [3:0] ALUOP,
  output Signed_Overflow,
  output Unsigned_overflow,
  output [31:0] Result,
  output [31:0] Result_2,
  output Equal
);

  // Probe on X
  // Probe on X
  ALU alu_1 (
    .AluOP(ALUOP), .X(X), .Equal(Equal), .Result(Result), .Signed_Overflow(Signed_Overflow), .Y(Y),
    .Result_2(Result_2), .UnSigned_Overflow(Unsigned_overflow));
  // Probe on ALUOP
  // Probe on Y
  // Probe on Y
  // Probe on Result
  // Probe on Result
  // Probe on Result_2
endmodule

module ADD (
  input  [31:0] X,
  input  [31:0] in_2,
  output [31:0] out,
  output CF,
  output OF
);

  wire adder_1_cout, adder_2_cout, adder_3_cout, and_1_out, and_2_out, not_1_out, not_2_out, not_3_out;

  not not_1 (not_1_out, X[31]);
  not not_2 (not_2_out, in_2[31]);
  not not_3 (not_3_out, out[31]);
  Adder adder_1 (.a(X[7:0]), .b(in_2[7:0]), .out(out[7:0]), .cin(1'b0), .cout(adder_1_cout));
  Adder adder_2 (.a(X[15:8]), .b(in_2[15:8]), .out(out[15:8]), .cin(adder_1_cout), .cout(adder_2_cout));
  Adder adder_3 (.a(X[23:16]), .b(in_2[23:16]), .out(out[23:16]), .cin(adder_2_cout), .cout(adder_3_cout));
  Adder adder_4 (.a(X[31:24]), .b(in_2[31:24]), .out(out[31:24]), .cin(adder_3_cout), .cout(CF));
  and and_1 (and_1_out, not_3_out, in_2[31], X[31]);
  and and_2 (and_2_out, out[31], not_1_out, not_2_out);
  or or_1 (OF, and_1_out, and_2_out);
endmodule

module SHL (
  input  [31:0] X,
  input  [31:0] Y,
  output [31:0] out_3
);

  Shifter #(.width(32)) shifter_1 (.in(X), .\dist (Y[4:0]), .out(out_3));
endmodule

module SHR (
  input  [31:0] X,
  input  [31:0] Y,
  output [31:0] out_3
);

  Shifter #(.width(32), .shift("lr")) shifter_1 (.in(X), .\dist (Y[4:0]), .out(out_3));
endmodule

module SAL (
  input  [31:0] X,
  input  [31:0] Y,
  output [31:0] out_3
);

  Shifter #(.width(32), .shift("ar")) shifter_1 (.in(X), .\dist (Y[4:0]), .out(out_3));
endmodule

module MUL (
  input  [31:0] X,
  input  [31:0] Y,
  output [31:0] Out1,
  output [31:0] Out2
);

  wire [31:0] bit_extender_1_out;

  assign bit_extender_1_out = {{31{1'b0}}, 1'b0};  // Bit_Extender bit_extender_1
  Multiplier #(.width(32)) multiplier_1 (.a(X), .b(Y), .out(Out1), .cin(bit_extender_1_out), .cout(Out2));
endmodule

module DIV (
  input  [31:0] X,
  input  [31:0] Y,
  output [31:0] Out1,
  output [31:0] Out2
);

  wire [31:0] bit_extender_1_out;

  assign bit_extender_1_out = {{31{1'b0}}, 1'b0};  // Bit_Extender bit_extender_1
  Divider #(.width(32)) divider_1 (.a(X), .b(Y), .out(Out1), .upper(bit_extender_1_out), .rem(Out2));
endmodule

module SUB (
  input  [31:0] X,
  input  [31:0] in_2,
  output [31:0] out,
  output CF,
  output OF
);

  wire subtractor_1_bout;

  Subtractor #(.width(31)) subtractor_1 (
    .a(X[30:0]), .b(in_2[30:0]), .out(out[30:0]), .bin(1'b0), .bout(subtractor_1_bout));
  Subtractor #(.width(1)) subtractor_2 (.a(X[31]), .b(in_2[31]), .out(out[31]), .bin(subtractor_1_bout), .bout(CF));
  xor xor_1 (OF, CF, subtractor_1_bout);
endmodule
