// Logisim project decoder.circ as structural Verilog: 1 circuit, main circuit InstrDecode
// InstrDecoder
module InstrDecode (
  input  [31:0] IND,
  output [4:0] rd,
  output [15:0] IMM,
  output [4:0] rt,
  output [5:0] Funct,
  output [4:0] rs,
  output [5:0] OpCode,
  output [25:0] Addr,
  output [4:0] shamt
);


  assign Addr = IND[25:0];
  assign Funct = IND[5:0];
  assign IMM = IND[15:0];
  assign OpCode = IND[31:26];
  assign rd = IND[15:11];
  assign rs = IND[25:21];
  assign rt = IND[20:16];
  assign shamt = IND[10:6];

  // Other names for the same wires on the sheet: op[5:0] = IND[31:26]
endmodule
