// Logisim project pc.circ as structural Verilog: 1 circuit, main circuit ProgramCounter
// PC
module ProgramCounter (
  input  Clk,
  input  Rst,
  input  [31:0] offset,
  output [23:0] Addr
);

  wire [31:0] adder_1_out, Reg_q;

  Adder #(.width(32)) adder_1 (.a({Reg_q[31:26], Addr, Reg_q[1:0]}), .b(offset), .out(adder_1_out));  // open: cin, cout
  // Probe on offset
  // Probe on offset
  // Probe on Addr
  // Probe on Addr
  Register #(.width(32)) Reg (.D(adder_1_out), .Q({Reg_q[31:26], Addr, Reg_q[1:0]}), .clk(Clk), .clr(Rst));  // open: en
endmodule
