// Logisim project regfile.circ as structural Verilog: 3 circuits, main circuit RegFile
module RegFile (
  input  [4:0] Reg1_num,
  input  [4:0] Reg2,
  input  [4:0] in_3,
  input  [4:0] Write_Reg_num,
  input  [31:0] Din,
  input  Write_Enable,
  input  Clock,
  output [31:0] Reg1,
  output [31:0] v0,
  output [31:0] a0,
  output [31:0] DebugValue,
  output [31:0] Reg2_2
);

  wire decoder_1_out0, decoder_1_out1, decoder_1_out2, decoder_1_out3, decoder_1_out4, decoder_1_out5,
       decoder_1_out6, decoder_1_out7, decoder_1_out8, decoder_1_out9, decoder_1_out10, decoder_1_out11,
       decoder_1_out12, decoder_1_out13, decoder_1_out14, decoder_1_out15, decoder_1_out16, decoder_1_out17,
       decoder_1_out18, decoder_1_out19, decoder_1_out20, decoder_1_out21, decoder_1_out22, decoder_1_out23,
       decoder_1_out24, decoder_1_out25, decoder_1_out26, decoder_1_out27, decoder_1_out28, decoder_1_out29,
       decoder_1_out30, decoder_1_out31;
  wire [31:0] _0_q, _1_q, _14_2_q, _14_3_q, _14_4_q, _14_5_q, _14_6_q, _14_7_q, _14_8_q, _14_9_q, _14_10_q,
       _14_11_q, _14_12_q, _14_13_q, _14_14_q, _14_15_q, _14_16_q, _14_17_q, _14_18_q, _14_19_q, _14_20_q,
       _14_21_q, _14_22_q, _14_q, _20_q, _22_q, _24_q, _26_q, _28_q, _30_q;

  Decoder #(.select(5), .disabled(0)) decoder_1 (
    .out0(decoder_1_out0), .out1(decoder_1_out1), .out2(decoder_1_out2), .out3(decoder_1_out3),
    .out4(decoder_1_out4), .out5(decoder_1_out5), .out6(decoder_1_out6), .out7(decoder_1_out7),
    .out8(decoder_1_out8), .out9(decoder_1_out9), .out10(decoder_1_out10), .out11(decoder_1_out11),
    .out12(decoder_1_out12), .out13(decoder_1_out13), .out14(decoder_1_out14), .out15(decoder_1_out15),
    .out16(decoder_1_out16), .out17(decoder_1_out17), .out18(decoder_1_out18), .out19(decoder_1_out19),
    .out20(decoder_1_out20), .out21(decoder_1_out21), .out22(decoder_1_out22), .out23(decoder_1_out23),
    .out24(decoder_1_out24), .out25(decoder_1_out25), .out26(decoder_1_out26), .out27(decoder_1_out27),
    .out28(decoder_1_out28), .out29(decoder_1_out29), .out30(decoder_1_out30), .out31(decoder_1_out31),
    .sel(Write_Reg_num), .en(Write_Enable));
  Multiplexer #(.select(5), .width(32), .enable("false")) multiplexer_1 (
    .in0(_0_q), .in1(_1_q), .in2(v0), .in3(_14_15_q), .in4(a0), .in5(_14_q), .in6(_14_8_q), .in7(_14_16_q),
    .in8(_20_q), .in9(_14_2_q), .in10(_14_9_q), .in11(_14_17_q), .in12(_22_q), .in13(_14_3_q),
    .in14(_14_10_q), .in15(_14_18_q), .in16(_24_q), .in17(_14_4_q), .in18(_14_11_q), .in19(_14_19_q),
    .in20(_26_q), .in21(_14_5_q), .in22(_14_12_q), .in23(_14_20_q), .in24(_28_q), .in25(_14_6_q),
    .in26(_14_13_q), .in27(_14_21_q), .in28(_30_q), .in29(_14_7_q), .in30(_14_14_q), .in31(_14_22_q),
    .out(DebugValue), .sel(in_3));
  Multiplexer #(.select(5), .width(32), .enable("false")) multiplexer_2 (
    .in0(_0_q), .in1(_1_q), .in2(v0), .in3(_14_15_q), .in4(a0), .in5(_14_q), .in6(_14_8_q), .in7(_14_16_q),
    .in8(_20_q), .in9(_14_2_q), .in10(_14_9_q), .in11(_14_17_q), .in12(_22_q), .in13(_14_3_q),
    .in14(_14_10_q), .in15(_14_18_q), .in16(_24_q), .in17(_14_4_q), .in18(_14_11_q), .in19(_14_19_q),
    .in20(_26_q), .in21(_14_5_q), .in22(_14_12_q), .in23(_14_20_q), .in24(_28_q), .in25(_14_6_q),
    .in26(_14_13_q), .in27(_14_21_q), .in28(_30_q), .in29(_14_7_q), .in30(_14_14_q), .in31(_14_22_q),
    .out(Reg1), .sel(Reg1_num));
  Register #(.width(32)) _0 (.D(Din), .en(decoder_1_out0), .Q(_0_q), .clk(Clock), .clr(1'b1));
  Register #(.width(32)) _18 (.D(Din), .en(decoder_1_out4), .Q(a0), .clk(Clock));  // open: clr
  Register #(.width(32)) _20 (.D(Din), .en(decoder_1_out8), .Q(_20_q), .clk(Clock));  // open: clr
  Register #(.width(32)) _22 (.D(Din), .en(decoder_1_out12), .Q(_22_q), .clk(Clock));  // open: clr
  Register #(.width(32)) _24 (.D(Din), .en(decoder_1_out16), .Q(_24_q), .clk(Clock));  // open: clr
  Register #(.width(32)) _26 (.D(Din), .en(decoder_1_out20), .Q(_26_q), .clk(Clock));  // open: clr
  Register #(.width(32)) _28 (.D(Din), .en(decoder_1_out24), .Q(_28_q), .clk(Clock));  // open: clr
  Register #(.width(32)) _30 (.D(Din), .en(decoder_1_out28), .Q(_30_q), .clk(Clock));  // open: clr
  Register #(.width(32)) _1 (.D(Din), .en(decoder_1_out1), .Q(_1_q), .clk(Clock));  // open: clr
  Register #(.width(32)) _14 (.D(Din), .en(decoder_1_out5), .Q(_14_q), .clk(Clock));  // open: clr
  Register #(.width(32)) _14_2 (.D(Din), .en(decoder_1_out9), .Q(_14_2_q), .clk(Clock));  // open: clr
  Register #(.width(32)) _14_3 (.D(Din), .en(decoder_1_out13), .Q(_14_3_q), .clk(Clock));  // open: clr
  Register #(.width(32)) _14_4 (.D(Din), .en(decoder_1_out17), .Q(_14_4_q), .clk(Clock));  // open: clr
  Register #(.width(32)) _14_5 (.D(Din), .en(decoder_1_out21), .Q(_14_5_q), .clk(Clock));  // open: clr
  Register #(.width(32)) _14_6 (.D(Din), .en(decoder_1_out25), .Q(_14_6_q), .clk(Clock));  // open: clr
  Register #(.width(32)) _14_7 (.D(Din), .en(decoder_1_out29), .Q(_14_7_q), .clk(Clock));  // open: clr
  Register #(.width(32)) _2 (.D(Din), .en(decoder_1_out2), .Q(v0), .clk(Clock));  // open: clr
  Register #(.width(32)) _14_8 (.D(Din), .en(decoder_1_out6), .Q(_14_8_q), .clk(Clock));  // open: clr
  Register #(.width(32)) _14_9 (.D(Din), .en(decoder_1_out10), .Q(_14_9_q), .clk(Clock));  // open: clr
  Register #(.width(32)) _14_10 (.D(Din), .en(decoder_1_out14), .Q(_14_10_q), .clk(Clock));  // open: clr
  Register #(.width(32)) _14_11 (.D(Din), .en(decoder_1_out18), .Q(_14_11_q), .clk(Clock));  // open: clr
  Register #(.width(32)) _14_12 (.D(Din), .en(decoder_1_out22), .Q(_14_12_q), .clk(Clock));  // open: clr
  Register #(.width(32)) _14_13 (.D(Din), .en(decoder_1_out26), .Q(_14_13_q), .clk(Clock));  // open: clr
  Register #(.width(32)) _14_14 (.D(Din), .en(decoder_1_out30), .Q(_14_14_q), .clk(Clock));  // open: clr
  Register #(.width(32)) _14_15 (.D(Din), .en(decoder_1_out3), .Q(_14_15_q), .clk(Clock));  // open: clr
  Register #(.width(32)) _14_16 (.D(Din), .en(decoder_1_out7), .Q(_14_16_q), .clk(Clock));  // open: clr
  Register #(.width(32)) _14_17 (.D(Din), .en(decoder_1_out11), .Q(_14_17_q), .clk(Clock));  // open: clr
  Register #(.width(32)) _14_18 (.D(Din), .en(decoder_1_out15), .Q(_14_18_q), .clk(Clock));  // open: clr
  Register #(.width(32)) _14_19 (.D(Din), .en(decoder_1_out19), .Q(_14_19_q), .clk(Clock));  // open: clr
  Register #(.width(32)) _14_20 (.D(Din), .en(decoder_1_out23), .Q(_14_20_q), .clk(Clock));  // open: clr
  Register #(.width(32)) _14_21 (.D(Din), .en(decoder_1_out27), .Q(_14_21_q), .clk(Clock));  // open: clr
  Register #(.width(32)) _14_22 (.D(Din), .en(decoder_1_out31), .Q(_14_22_q), .clk(Clock));  // open: clr
  Multiplexer #(.select(5), .width(32), .enable("false")) multiplexer_3 (
    .in0(_0_q), .in1(_1_q), .in2(v0), .in3(_14_15_q), .in4(a0), .in5(_14_q), .in6(_14_8_q), .in7(_14_16_q),
    .in8(_20_q), .in9(_14_2_q), .in10(_14_9_q), .in11(_14_17_q), .in12(_22_q), .in13(_14_3_q),
    .in14(_14_10_q), .in15(_14_18_q), .in16(_24_q), .in17(_14_4_q), .in18(_14_11_q), .in19(_14_19_q),
    .in20(_26_q), .in21(_14_5_q), .in22(_14_12_q), .in23(_14_20_q), .in24(_28_q), .in25(_14_6_q),
    .in26(_14_13_q), .in27(_14_21_q), .in28(_30_q), .in29(_14_7_q), .in30(_14_14_q), .in31(_14_22_q),
    .out(Reg2_2), .sel(Reg2));

  // Other names for the same wires on the sheet: clk = Clock; Debug[31:0] = DebugValue; Debug_t[4:0] = in_3;
  //   reg2_num[4:0] = Reg2; reg2_t[31:0] = Reg2_2; WE = Write_Enable; write_data[31:0] = Din

  // Notes on the sheet:
  //   输入引脚
  //   输出引脚
  //   Debug引脚，便于观测寄存器值
  //   请勿修改引脚以及封装，直接使用隧道连接电路
endmodule

module HILO (
  input  [31:0] HI_In,
  input  [31:0] LO_In,
  input  Clk,
  input  Control,
  output [31:0] HI_Out,
  output [31:0] LO_Out
);

  wire and_1_out;

  Register #(.width(32)) HI (.D(HI_In), .Q(HI_Out), .clk(and_1_out));  // open: en, clr
  and and_1 (and_1_out, Clk, Control);
  Register #(.width(32)) LO (.D(LO_In), .Q(LO_Out), .clk(and_1_out));  // open: en, clr
  // Probe on HI_Out
  // Probe on HI_Out
  // Probe on LO_Out
  // Probe on LO_Out
endmodule

module HILOControl (
  input  [3:0] ALUop,
  output HILOControl
);

  wire and_1_out, and_2_out, not_1_out, not_2_out, not_3_out, not_4_out;

  not not_1 (not_1_out, ALUop[0]);
  not not_2 (not_2_out, ALUop[1]);
  not not_3 (not_3_out, ALUop[2]);
  not not_4 (not_4_out, ALUop[3]);
  and and_1 (and_1_out, not_4_out, not_3_out, ALUop[1], ALUop[0]);
  and and_2 (and_2_out, not_4_out, ALUop[2], not_2_out, not_1_out);
  or or_1 (HILOControl, and_1_out, and_2_out);
endmodule
